// Logisim project CPU_Design2.circ as structural Verilog: 6 circuits, main circuit RegisterFile
module main (
  input  Clock,
  input  [31:0] in_2,
  input  Enable_C,
  input  [4:0] Add_C,
  input  Enable_Add_C,
  input  [4:0] Add_A,
  input  [4:0] Add_B,
  output [31:0] A_value,
  output [31:0] B_value
);

  wire demultiplexer_1_out0, demultiplexer_1_out1, demultiplexer_1_out2, demultiplexer_1_out3,
       demultiplexer_1_out4, demultiplexer_1_out5, demultiplexer_1_out6, demultiplexer_1_out7,
       demultiplexer_1_out8, demultiplexer_1_out9, demultiplexer_1_out10, demultiplexer_1_out11,
       demultiplexer_1_out12, demultiplexer_1_out13, demultiplexer_1_out14, demultiplexer_1_out15,
       demultiplexer_1_out16, demultiplexer_1_out17, demultiplexer_1_out18, demultiplexer_1_out19,
       demultiplexer_1_out20, demultiplexer_1_out21, demultiplexer_1_out22, demultiplexer_1_out23,
       demultiplexer_1_out24, demultiplexer_1_out25, demultiplexer_1_out26, demultiplexer_1_out27,
       demultiplexer_1_out28, demultiplexer_1_out29, demultiplexer_1_out30, demultiplexer_1_out31,
       multiplexer_1_out, not_1_out;
  wire [31:0] demultiplexer_2_out0, demultiplexer_2_out1, demultiplexer_2_out2, demultiplexer_2_out3,
       demultiplexer_2_out4, demultiplexer_2_out5, demultiplexer_2_out6, demultiplexer_2_out7,
       demultiplexer_2_out8, demultiplexer_2_out9, demultiplexer_2_out10, demultiplexer_2_out11,
       demultiplexer_2_out12, demultiplexer_2_out13, demultiplexer_2_out14, demultiplexer_2_out15,
       demultiplexer_2_out16, demultiplexer_2_out17, demultiplexer_2_out18, demultiplexer_2_out19,
       demultiplexer_2_out20, demultiplexer_2_out21, demultiplexer_2_out22, demultiplexer_2_out23,
       demultiplexer_2_out24, demultiplexer_2_out25, demultiplexer_2_out26, demultiplexer_2_out27,
       demultiplexer_2_out28, demultiplexer_2_out29, demultiplexer_2_out30, demultiplexer_2_out31, R0_q31,
       R1_q31, R2_q31, R3_q31, R4_q31, R5_q31, R6_q31, R7_q31, R8_q31, R9_q31, R10_q31, R11_q31, R12_q31,
       R13_q31, R14_q31, R15_q31, R16_q31, R17_q31, R18_q31, R19_q31, R20_q31, R21_q31, R22_q31, R23_q31,
       R24_q31, R25_q31, R26_q31, R27_q31, R28_q31, R29_q31, R30_q31, R31_q31;

  Multiplexer #(.enable("false")) multiplexer_1 (
    .in0(1'b0), .in1(not_1_out), .out(multiplexer_1_out), .sel(Enable_Add_C));
  Demultiplexer #(.select(5), .enable("false")) demultiplexer_1 (
    .out0(demultiplexer_1_out0), .out1(demultiplexer_1_out1), .out2(demultiplexer_1_out2),
    .out3(demultiplexer_1_out3), .out4(demultiplexer_1_out4), .out5(demultiplexer_1_out5),
    .out6(demultiplexer_1_out6), .out7(demultiplexer_1_out7), .out8(demultiplexer_1_out8),
    .out9(demultiplexer_1_out9), .out10(demultiplexer_1_out10), .out11(demultiplexer_1_out11),
    .out12(demultiplexer_1_out12), .out13(demultiplexer_1_out13), .out14(demultiplexer_1_out14),
    .out15(demultiplexer_1_out15), .out16(demultiplexer_1_out16), .out17(demultiplexer_1_out17),
    .out18(demultiplexer_1_out18), .out19(demultiplexer_1_out19), .out20(demultiplexer_1_out20),
    .out21(demultiplexer_1_out21), .out22(demultiplexer_1_out22), .out23(demultiplexer_1_out23),
    .out24(demultiplexer_1_out24), .out25(demultiplexer_1_out25), .out26(demultiplexer_1_out26),
    .out27(demultiplexer_1_out27), .out28(demultiplexer_1_out28), .out29(demultiplexer_1_out29),
    .out30(demultiplexer_1_out30), .out31(demultiplexer_1_out31), .in(multiplexer_1_out), .sel(Add_C));
  not not_1 (not_1_out, 1'b0);
  Shift_Register #(.length(32)) R0 (
    .shift(1'b0), .clk(Clock), .load(demultiplexer_1_out0), .d0(demultiplexer_2_out0[31]), .q0(R0_q31[31]),
    .d1(demultiplexer_2_out0[30]), .q1(R0_q31[30]), .d2(demultiplexer_2_out0[29]), .q2(R0_q31[29]),
    .d3(demultiplexer_2_out0[28]), .q3(R0_q31[28]), .d4(demultiplexer_2_out0[27]), .q4(R0_q31[27]),
    .d5(demultiplexer_2_out0[26]), .q5(R0_q31[26]), .d6(demultiplexer_2_out0[25]), .q6(R0_q31[25]),
    .d7(demultiplexer_2_out0[24]), .q7(R0_q31[24]), .d8(demultiplexer_2_out0[23]), .q8(R0_q31[23]),
    .d9(demultiplexer_2_out0[22]), .q9(R0_q31[22]), .d10(demultiplexer_2_out0[21]), .q10(R0_q31[21]),
    .d11(demultiplexer_2_out0[20]), .q11(R0_q31[20]), .d12(demultiplexer_2_out0[19]), .q12(R0_q31[19]),
    .d13(demultiplexer_2_out0[18]), .q13(R0_q31[18]), .d14(demultiplexer_2_out0[17]), .q14(R0_q31[17]),
    .d15(demultiplexer_2_out0[16]), .q15(R0_q31[16]), .d16(demultiplexer_2_out0[15]), .q16(R0_q31[15]),
    .d17(demultiplexer_2_out0[14]), .q17(R0_q31[14]), .d18(demultiplexer_2_out0[13]), .q18(R0_q31[13]),
    .d19(demultiplexer_2_out0[12]), .q19(R0_q31[12]), .d20(demultiplexer_2_out0[11]), .q20(R0_q31[11]),
    .d21(demultiplexer_2_out0[10]), .q21(R0_q31[10]), .d22(demultiplexer_2_out0[9]), .q22(R0_q31[9]),
    .d23(demultiplexer_2_out0[8]), .q23(R0_q31[8]), .d24(demultiplexer_2_out0[7]), .q24(R0_q31[7]),
    .d25(demultiplexer_2_out0[6]), .q25(R0_q31[6]), .d26(demultiplexer_2_out0[5]), .q26(R0_q31[5]),
    .d27(demultiplexer_2_out0[4]), .q27(R0_q31[4]), .d28(demultiplexer_2_out0[3]), .q28(R0_q31[3]),
    .d29(demultiplexer_2_out0[2]), .q29(R0_q31[2]), .d30(demultiplexer_2_out0[1]), .q30(R0_q31[1]),
    .d31(demultiplexer_2_out0[0]), .q31(R0_q31[0]));  // open: in, out, clr
  Shift_Register #(.length(32)) R1 (
    .shift(1'b0), .clk(Clock), .load(demultiplexer_1_out1), .d0(demultiplexer_2_out1[31]), .q0(R1_q31[31]),
    .d1(demultiplexer_2_out1[30]), .q1(R1_q31[30]), .d2(demultiplexer_2_out1[29]), .q2(R1_q31[29]),
    .d3(demultiplexer_2_out1[28]), .q3(R1_q31[28]), .d4(demultiplexer_2_out1[27]), .q4(R1_q31[27]),
    .d5(demultiplexer_2_out1[26]), .q5(R1_q31[26]), .d6(demultiplexer_2_out1[25]), .q6(R1_q31[25]),
    .d7(demultiplexer_2_out1[24]), .q7(R1_q31[24]), .d8(demultiplexer_2_out1[23]), .q8(R1_q31[23]),
    .d9(demultiplexer_2_out1[22]), .q9(R1_q31[22]), .d10(demultiplexer_2_out1[21]), .q10(R1_q31[21]),
    .d11(demultiplexer_2_out1[20]), .q11(R1_q31[20]), .d12(demultiplexer_2_out1[19]), .q12(R1_q31[19]),
    .d13(demultiplexer_2_out1[18]), .q13(R1_q31[18]), .d14(demultiplexer_2_out1[17]), .q14(R1_q31[17]),
    .d15(demultiplexer_2_out1[16]), .q15(R1_q31[16]), .d16(demultiplexer_2_out1[15]), .q16(R1_q31[15]),
    .d17(demultiplexer_2_out1[14]), .q17(R1_q31[14]), .d18(demultiplexer_2_out1[13]), .q18(R1_q31[13]),
    .d19(demultiplexer_2_out1[12]), .q19(R1_q31[12]), .d20(demultiplexer_2_out1[11]), .q20(R1_q31[11]),
    .d21(demultiplexer_2_out1[10]), .q21(R1_q31[10]), .d22(demultiplexer_2_out1[9]), .q22(R1_q31[9]),
    .d23(demultiplexer_2_out1[8]), .q23(R1_q31[8]), .d24(demultiplexer_2_out1[7]), .q24(R1_q31[7]),
    .d25(demultiplexer_2_out1[6]), .q25(R1_q31[6]), .d26(demultiplexer_2_out1[5]), .q26(R1_q31[5]),
    .d27(demultiplexer_2_out1[4]), .q27(R1_q31[4]), .d28(demultiplexer_2_out1[3]), .q28(R1_q31[3]),
    .d29(demultiplexer_2_out1[2]), .q29(R1_q31[2]), .d30(demultiplexer_2_out1[1]), .q30(R1_q31[1]),
    .d31(demultiplexer_2_out1[0]), .q31(R1_q31[0]));  // open: in, out, clr
  Shift_Register #(.length(32)) R2 (
    .shift(1'b0), .clk(Clock), .load(demultiplexer_1_out2), .d0(demultiplexer_2_out2[31]), .q0(R2_q31[31]),
    .d1(demultiplexer_2_out2[30]), .q1(R2_q31[30]), .d2(demultiplexer_2_out2[29]), .q2(R2_q31[29]),
    .d3(demultiplexer_2_out2[28]), .q3(R2_q31[28]), .d4(demultiplexer_2_out2[27]), .q4(R2_q31[27]),
    .d5(demultiplexer_2_out2[26]), .q5(R2_q31[26]), .d6(demultiplexer_2_out2[25]), .q6(R2_q31[25]),
    .d7(demultiplexer_2_out2[24]), .q7(R2_q31[24]), .d8(demultiplexer_2_out2[23]), .q8(R2_q31[23]),
    .d9(demultiplexer_2_out2[22]), .q9(R2_q31[22]), .d10(demultiplexer_2_out2[21]), .q10(R2_q31[21]),
    .d11(demultiplexer_2_out2[20]), .q11(R2_q31[20]), .d12(demultiplexer_2_out2[19]), .q12(R2_q31[19]),
    .d13(demultiplexer_2_out2[18]), .q13(R2_q31[18]), .d14(demultiplexer_2_out2[17]), .q14(R2_q31[17]),
    .d15(demultiplexer_2_out2[16]), .q15(R2_q31[16]), .d16(demultiplexer_2_out2[15]), .q16(R2_q31[15]),
    .d17(demultiplexer_2_out2[14]), .q17(R2_q31[14]), .d18(demultiplexer_2_out2[13]), .q18(R2_q31[13]),
    .d19(demultiplexer_2_out2[12]), .q19(R2_q31[12]), .d20(demultiplexer_2_out2[11]), .q20(R2_q31[11]),
    .d21(demultiplexer_2_out2[10]), .q21(R2_q31[10]), .d22(demultiplexer_2_out2[9]), .q22(R2_q31[9]),
    .d23(demultiplexer_2_out2[8]), .q23(R2_q31[8]), .d24(demultiplexer_2_out2[7]), .q24(R2_q31[7]),
    .d25(demultiplexer_2_out2[6]), .q25(R2_q31[6]), .d26(demultiplexer_2_out2[5]), .q26(R2_q31[5]),
    .d27(demultiplexer_2_out2[4]), .q27(R2_q31[4]), .d28(demultiplexer_2_out2[3]), .q28(R2_q31[3]),
    .d29(demultiplexer_2_out2[2]), .q29(R2_q31[2]), .d30(demultiplexer_2_out2[1]), .q30(R2_q31[1]),
    .d31(demultiplexer_2_out2[0]), .q31(R2_q31[0]));  // open: in, out, clr
  Shift_Register #(.length(32)) R3 (
    .shift(1'b0), .clk(Clock), .load(demultiplexer_1_out3), .d0(demultiplexer_2_out3[31]), .q0(R3_q31[31]),
    .d1(demultiplexer_2_out3[30]), .q1(R3_q31[30]), .d2(demultiplexer_2_out3[29]), .q2(R3_q31[29]),
    .d3(demultiplexer_2_out3[28]), .q3(R3_q31[28]), .d4(demultiplexer_2_out3[27]), .q4(R3_q31[27]),
    .d5(demultiplexer_2_out3[26]), .q5(R3_q31[26]), .d6(demultiplexer_2_out3[25]), .q6(R3_q31[25]),
    .d7(demultiplexer_2_out3[24]), .q7(R3_q31[24]), .d8(demultiplexer_2_out3[23]), .q8(R3_q31[23]),
    .d9(demultiplexer_2_out3[22]), .q9(R3_q31[22]), .d10(demultiplexer_2_out3[21]), .q10(R3_q31[21]),
    .d11(demultiplexer_2_out3[20]), .q11(R3_q31[20]), .d12(demultiplexer_2_out3[19]), .q12(R3_q31[19]),
    .d13(demultiplexer_2_out3[18]), .q13(R3_q31[18]), .d14(demultiplexer_2_out3[17]), .q14(R3_q31[17]),
    .d15(demultiplexer_2_out3[16]), .q15(R3_q31[16]), .d16(demultiplexer_2_out3[15]), .q16(R3_q31[15]),
    .d17(demultiplexer_2_out3[14]), .q17(R3_q31[14]), .d18(demultiplexer_2_out3[13]), .q18(R3_q31[13]),
    .d19(demultiplexer_2_out3[12]), .q19(R3_q31[12]), .d20(demultiplexer_2_out3[11]), .q20(R3_q31[11]),
    .d21(demultiplexer_2_out3[10]), .q21(R3_q31[10]), .d22(demultiplexer_2_out3[9]), .q22(R3_q31[9]),
    .d23(demultiplexer_2_out3[8]), .q23(R3_q31[8]), .d24(demultiplexer_2_out3[7]), .q24(R3_q31[7]),
    .d25(demultiplexer_2_out3[6]), .q25(R3_q31[6]), .d26(demultiplexer_2_out3[5]), .q26(R3_q31[5]),
    .d27(demultiplexer_2_out3[4]), .q27(R3_q31[4]), .d28(demultiplexer_2_out3[3]), .q28(R3_q31[3]),
    .d29(demultiplexer_2_out3[2]), .q29(R3_q31[2]), .d30(demultiplexer_2_out3[1]), .q30(R3_q31[1]),
    .d31(demultiplexer_2_out3[0]), .q31(R3_q31[0]));  // open: in, out, clr
  Shift_Register #(.length(32)) R4 (
    .shift(1'b0), .clk(Clock), .load(demultiplexer_1_out4), .d0(demultiplexer_2_out4[31]), .q0(R4_q31[31]),
    .d1(demultiplexer_2_out4[30]), .q1(R4_q31[30]), .d2(demultiplexer_2_out4[29]), .q2(R4_q31[29]),
    .d3(demultiplexer_2_out4[28]), .q3(R4_q31[28]), .d4(demultiplexer_2_out4[27]), .q4(R4_q31[27]),
    .d5(demultiplexer_2_out4[26]), .q5(R4_q31[26]), .d6(demultiplexer_2_out4[25]), .q6(R4_q31[25]),
    .d7(demultiplexer_2_out4[24]), .q7(R4_q31[24]), .d8(demultiplexer_2_out4[23]), .q8(R4_q31[23]),
    .d9(demultiplexer_2_out4[22]), .q9(R4_q31[22]), .d10(demultiplexer_2_out4[21]), .q10(R4_q31[21]),
    .d11(demultiplexer_2_out4[20]), .q11(R4_q31[20]), .d12(demultiplexer_2_out4[19]), .q12(R4_q31[19]),
    .d13(demultiplexer_2_out4[18]), .q13(R4_q31[18]), .d14(demultiplexer_2_out4[17]), .q14(R4_q31[17]),
    .d15(demultiplexer_2_out4[16]), .q15(R4_q31[16]), .d16(demultiplexer_2_out4[15]), .q16(R4_q31[15]),
    .d17(demultiplexer_2_out4[14]), .q17(R4_q31[14]), .d18(demultiplexer_2_out4[13]), .q18(R4_q31[13]),
    .d19(demultiplexer_2_out4[12]), .q19(R4_q31[12]), .d20(demultiplexer_2_out4[11]), .q20(R4_q31[11]),
    .d21(demultiplexer_2_out4[10]), .q21(R4_q31[10]), .d22(demultiplexer_2_out4[9]), .q22(R4_q31[9]),
    .d23(demultiplexer_2_out4[8]), .q23(R4_q31[8]), .d24(demultiplexer_2_out4[7]), .q24(R4_q31[7]),
    .d25(demultiplexer_2_out4[6]), .q25(R4_q31[6]), .d26(demultiplexer_2_out4[5]), .q26(R4_q31[5]),
    .d27(demultiplexer_2_out4[4]), .q27(R4_q31[4]), .d28(demultiplexer_2_out4[3]), .q28(R4_q31[3]),
    .d29(demultiplexer_2_out4[2]), .q29(R4_q31[2]), .d30(demultiplexer_2_out4[1]), .q30(R4_q31[1]),
    .d31(demultiplexer_2_out4[0]), .q31(R4_q31[0]));  // open: in, out, clr
  Shift_Register #(.length(32)) R5 (
    .shift(1'b0), .clk(Clock), .load(demultiplexer_1_out5), .d0(demultiplexer_2_out5[31]), .q0(R5_q31[31]),
    .d1(demultiplexer_2_out5[30]), .q1(R5_q31[30]), .d2(demultiplexer_2_out5[29]), .q2(R5_q31[29]),
    .d3(demultiplexer_2_out5[28]), .q3(R5_q31[28]), .d4(demultiplexer_2_out5[27]), .q4(R5_q31[27]),
    .d5(demultiplexer_2_out5[26]), .q5(R5_q31[26]), .d6(demultiplexer_2_out5[25]), .q6(R5_q31[25]),
    .d7(demultiplexer_2_out5[24]), .q7(R5_q31[24]), .d8(demultiplexer_2_out5[23]), .q8(R5_q31[23]),
    .d9(demultiplexer_2_out5[22]), .q9(R5_q31[22]), .d10(demultiplexer_2_out5[21]), .q10(R5_q31[21]),
    .d11(demultiplexer_2_out5[20]), .q11(R5_q31[20]), .d12(demultiplexer_2_out5[19]), .q12(R5_q31[19]),
    .d13(demultiplexer_2_out5[18]), .q13(R5_q31[18]), .d14(demultiplexer_2_out5[17]), .q14(R5_q31[17]),
    .d15(demultiplexer_2_out5[16]), .q15(R5_q31[16]), .d16(demultiplexer_2_out5[15]), .q16(R5_q31[15]),
    .d17(demultiplexer_2_out5[14]), .q17(R5_q31[14]), .d18(demultiplexer_2_out5[13]), .q18(R5_q31[13]),
    .d19(demultiplexer_2_out5[12]), .q19(R5_q31[12]), .d20(demultiplexer_2_out5[11]), .q20(R5_q31[11]),
    .d21(demultiplexer_2_out5[10]), .q21(R5_q31[10]), .d22(demultiplexer_2_out5[9]), .q22(R5_q31[9]),
    .d23(demultiplexer_2_out5[8]), .q23(R5_q31[8]), .d24(demultiplexer_2_out5[7]), .q24(R5_q31[7]),
    .d25(demultiplexer_2_out5[6]), .q25(R5_q31[6]), .d26(demultiplexer_2_out5[5]), .q26(R5_q31[5]),
    .d27(demultiplexer_2_out5[4]), .q27(R5_q31[4]), .d28(demultiplexer_2_out5[3]), .q28(R5_q31[3]),
    .d29(demultiplexer_2_out5[2]), .q29(R5_q31[2]), .d30(demultiplexer_2_out5[1]), .q30(R5_q31[1]),
    .d31(demultiplexer_2_out5[0]), .q31(R5_q31[0]));  // open: in, out, clr
  Shift_Register #(.length(32)) R6 (
    .shift(1'b0), .clk(Clock), .load(demultiplexer_1_out6), .d0(demultiplexer_2_out6[31]), .q0(R6_q31[31]),
    .d1(demultiplexer_2_out6[30]), .q1(R6_q31[30]), .d2(demultiplexer_2_out6[29]), .q2(R6_q31[29]),
    .d3(demultiplexer_2_out6[28]), .q3(R6_q31[28]), .d4(demultiplexer_2_out6[27]), .q4(R6_q31[27]),
    .d5(demultiplexer_2_out6[26]), .q5(R6_q31[26]), .d6(demultiplexer_2_out6[25]), .q6(R6_q31[25]),
    .d7(demultiplexer_2_out6[24]), .q7(R6_q31[24]), .d8(demultiplexer_2_out6[23]), .q8(R6_q31[23]),
    .d9(demultiplexer_2_out6[22]), .q9(R6_q31[22]), .d10(demultiplexer_2_out6[21]), .q10(R6_q31[21]),
    .d11(demultiplexer_2_out6[20]), .q11(R6_q31[20]), .d12(demultiplexer_2_out6[19]), .q12(R6_q31[19]),
    .d13(demultiplexer_2_out6[18]), .q13(R6_q31[18]), .d14(demultiplexer_2_out6[17]), .q14(R6_q31[17]),
    .d15(demultiplexer_2_out6[16]), .q15(R6_q31[16]), .d16(demultiplexer_2_out6[15]), .q16(R6_q31[15]),
    .d17(demultiplexer_2_out6[14]), .q17(R6_q31[14]), .d18(demultiplexer_2_out6[13]), .q18(R6_q31[13]),
    .d19(demultiplexer_2_out6[12]), .q19(R6_q31[12]), .d20(demultiplexer_2_out6[11]), .q20(R6_q31[11]),
    .d21(demultiplexer_2_out6[10]), .q21(R6_q31[10]), .d22(demultiplexer_2_out6[9]), .q22(R6_q31[9]),
    .d23(demultiplexer_2_out6[8]), .q23(R6_q31[8]), .d24(demultiplexer_2_out6[7]), .q24(R6_q31[7]),
    .d25(demultiplexer_2_out6[6]), .q25(R6_q31[6]), .d26(demultiplexer_2_out6[5]), .q26(R6_q31[5]),
    .d27(demultiplexer_2_out6[4]), .q27(R6_q31[4]), .d28(demultiplexer_2_out6[3]), .q28(R6_q31[3]),
    .d29(demultiplexer_2_out6[2]), .q29(R6_q31[2]), .d30(demultiplexer_2_out6[1]), .q30(R6_q31[1]),
    .d31(demultiplexer_2_out6[0]), .q31(R6_q31[0]));  // open: in, out, clr
  Shift_Register #(.length(32)) R7 (
    .shift(1'b0), .clk(Clock), .load(demultiplexer_1_out7), .d0(demultiplexer_2_out7[31]), .q0(R7_q31[31]),
    .d1(demultiplexer_2_out7[30]), .q1(R7_q31[30]), .d2(demultiplexer_2_out7[29]), .q2(R7_q31[29]),
    .d3(demultiplexer_2_out7[28]), .q3(R7_q31[28]), .d4(demultiplexer_2_out7[27]), .q4(R7_q31[27]),
    .d5(demultiplexer_2_out7[26]), .q5(R7_q31[26]), .d6(demultiplexer_2_out7[25]), .q6(R7_q31[25]),
    .d7(demultiplexer_2_out7[24]), .q7(R7_q31[24]), .d8(demultiplexer_2_out7[23]), .q8(R7_q31[23]),
    .d9(demultiplexer_2_out7[22]), .q9(R7_q31[22]), .d10(demultiplexer_2_out7[21]), .q10(R7_q31[21]),
    .d11(demultiplexer_2_out7[20]), .q11(R7_q31[20]), .d12(demultiplexer_2_out7[19]), .q12(R7_q31[19]),
    .d13(demultiplexer_2_out7[18]), .q13(R7_q31[18]), .d14(demultiplexer_2_out7[17]), .q14(R7_q31[17]),
    .d15(demultiplexer_2_out7[16]), .q15(R7_q31[16]), .d16(demultiplexer_2_out7[15]), .q16(R7_q31[15]),
    .d17(demultiplexer_2_out7[14]), .q17(R7_q31[14]), .d18(demultiplexer_2_out7[13]), .q18(R7_q31[13]),
    .d19(demultiplexer_2_out7[12]), .q19(R7_q31[12]), .d20(demultiplexer_2_out7[11]), .q20(R7_q31[11]),
    .d21(demultiplexer_2_out7[10]), .q21(R7_q31[10]), .d22(demultiplexer_2_out7[9]), .q22(R7_q31[9]),
    .d23(demultiplexer_2_out7[8]), .q23(R7_q31[8]), .d24(demultiplexer_2_out7[7]), .q24(R7_q31[7]),
    .d25(demultiplexer_2_out7[6]), .q25(R7_q31[6]), .d26(demultiplexer_2_out7[5]), .q26(R7_q31[5]),
    .d27(demultiplexer_2_out7[4]), .q27(R7_q31[4]), .d28(demultiplexer_2_out7[3]), .q28(R7_q31[3]),
    .d29(demultiplexer_2_out7[2]), .q29(R7_q31[2]), .d30(demultiplexer_2_out7[1]), .q30(R7_q31[1]),
    .d31(demultiplexer_2_out7[0]), .q31(R7_q31[0]));  // open: in, out, clr
  Shift_Register #(.length(32)) R8 (
    .shift(1'b0), .clk(Clock), .load(demultiplexer_1_out8), .d0(demultiplexer_2_out8[31]), .q0(R8_q31[31]),
    .d1(demultiplexer_2_out8[30]), .q1(R8_q31[30]), .d2(demultiplexer_2_out8[29]), .q2(R8_q31[29]),
    .d3(demultiplexer_2_out8[28]), .q3(R8_q31[28]), .d4(demultiplexer_2_out8[27]), .q4(R8_q31[27]),
    .d5(demultiplexer_2_out8[26]), .q5(R8_q31[26]), .d6(demultiplexer_2_out8[25]), .q6(R8_q31[25]),
    .d7(demultiplexer_2_out8[24]), .q7(R8_q31[24]), .d8(demultiplexer_2_out8[23]), .q8(R8_q31[23]),
    .d9(demultiplexer_2_out8[22]), .q9(R8_q31[22]), .d10(demultiplexer_2_out8[21]), .q10(R8_q31[21]),
    .d11(demultiplexer_2_out8[20]), .q11(R8_q31[20]), .d12(demultiplexer_2_out8[19]), .q12(R8_q31[19]),
    .d13(demultiplexer_2_out8[18]), .q13(R8_q31[18]), .d14(demultiplexer_2_out8[17]), .q14(R8_q31[17]),
    .d15(demultiplexer_2_out8[16]), .q15(R8_q31[16]), .d16(demultiplexer_2_out8[15]), .q16(R8_q31[15]),
    .d17(demultiplexer_2_out8[14]), .q17(R8_q31[14]), .d18(demultiplexer_2_out8[13]), .q18(R8_q31[13]),
    .d19(demultiplexer_2_out8[12]), .q19(R8_q31[12]), .d20(demultiplexer_2_out8[11]), .q20(R8_q31[11]),
    .d21(demultiplexer_2_out8[10]), .q21(R8_q31[10]), .d22(demultiplexer_2_out8[9]), .q22(R8_q31[9]),
    .d23(demultiplexer_2_out8[8]), .q23(R8_q31[8]), .d24(demultiplexer_2_out8[7]), .q24(R8_q31[7]),
    .d25(demultiplexer_2_out8[6]), .q25(R8_q31[6]), .d26(demultiplexer_2_out8[5]), .q26(R8_q31[5]),
    .d27(demultiplexer_2_out8[4]), .q27(R8_q31[4]), .d28(demultiplexer_2_out8[3]), .q28(R8_q31[3]),
    .d29(demultiplexer_2_out8[2]), .q29(R8_q31[2]), .d30(demultiplexer_2_out8[1]), .q30(R8_q31[1]),
    .d31(demultiplexer_2_out8[0]), .q31(R8_q31[0]));  // open: in, out, clr
  Shift_Register #(.length(32)) R9 (
    .shift(1'b0), .clk(Clock), .load(demultiplexer_1_out9), .d0(demultiplexer_2_out9[31]), .q0(R9_q31[31]),
    .d1(demultiplexer_2_out9[30]), .q1(R9_q31[30]), .d2(demultiplexer_2_out9[29]), .q2(R9_q31[29]),
    .d3(demultiplexer_2_out9[28]), .q3(R9_q31[28]), .d4(demultiplexer_2_out9[27]), .q4(R9_q31[27]),
    .d5(demultiplexer_2_out9[26]), .q5(R9_q31[26]), .d6(demultiplexer_2_out9[25]), .q6(R9_q31[25]),
    .d7(demultiplexer_2_out9[24]), .q7(R9_q31[24]), .d8(demultiplexer_2_out9[23]), .q8(R9_q31[23]),
    .d9(demultiplexer_2_out9[22]), .q9(R9_q31[22]), .d10(demultiplexer_2_out9[21]), .q10(R9_q31[21]),
    .d11(demultiplexer_2_out9[20]), .q11(R9_q31[20]), .d12(demultiplexer_2_out9[19]), .q12(R9_q31[19]),
    .d13(demultiplexer_2_out9[18]), .q13(R9_q31[18]), .d14(demultiplexer_2_out9[17]), .q14(R9_q31[17]),
    .d15(demultiplexer_2_out9[16]), .q15(R9_q31[16]), .d16(demultiplexer_2_out9[15]), .q16(R9_q31[15]),
    .d17(demultiplexer_2_out9[14]), .q17(R9_q31[14]), .d18(demultiplexer_2_out9[13]), .q18(R9_q31[13]),
    .d19(demultiplexer_2_out9[12]), .q19(R9_q31[12]), .d20(demultiplexer_2_out9[11]), .q20(R9_q31[11]),
    .d21(demultiplexer_2_out9[10]), .q21(R9_q31[10]), .d22(demultiplexer_2_out9[9]), .q22(R9_q31[9]),
    .d23(demultiplexer_2_out9[8]), .q23(R9_q31[8]), .d24(demultiplexer_2_out9[7]), .q24(R9_q31[7]),
    .d25(demultiplexer_2_out9[6]), .q25(R9_q31[6]), .d26(demultiplexer_2_out9[5]), .q26(R9_q31[5]),
    .d27(demultiplexer_2_out9[4]), .q27(R9_q31[4]), .d28(demultiplexer_2_out9[3]), .q28(R9_q31[3]),
    .d29(demultiplexer_2_out9[2]), .q29(R9_q31[2]), .d30(demultiplexer_2_out9[1]), .q30(R9_q31[1]),
    .d31(demultiplexer_2_out9[0]), .q31(R9_q31[0]));  // open: in, out, clr
  Shift_Register #(.length(32)) R10 (
    .shift(1'b0), .clk(Clock), .load(demultiplexer_1_out10), .d0(demultiplexer_2_out10[31]),
    .q0(R10_q31[31]), .d1(demultiplexer_2_out10[30]), .q1(R10_q31[30]), .d2(demultiplexer_2_out10[29]),
    .q2(R10_q31[29]), .d3(demultiplexer_2_out10[28]), .q3(R10_q31[28]), .d4(demultiplexer_2_out10[27]),
    .q4(R10_q31[27]), .d5(demultiplexer_2_out10[26]), .q5(R10_q31[26]), .d6(demultiplexer_2_out10[25]),
    .q6(R10_q31[25]), .d7(demultiplexer_2_out10[24]), .q7(R10_q31[24]), .d8(demultiplexer_2_out10[23]),
    .q8(R10_q31[23]), .d9(demultiplexer_2_out10[22]), .q9(R10_q31[22]), .d10(demultiplexer_2_out10[21]),
    .q10(R10_q31[21]), .d11(demultiplexer_2_out10[20]), .q11(R10_q31[20]), .d12(demultiplexer_2_out10[19]),
    .q12(R10_q31[19]), .d13(demultiplexer_2_out10[18]), .q13(R10_q31[18]), .d14(demultiplexer_2_out10[17]),
    .q14(R10_q31[17]), .d15(demultiplexer_2_out10[16]), .q15(R10_q31[16]), .d16(demultiplexer_2_out10[15]),
    .q16(R10_q31[15]), .d17(demultiplexer_2_out10[14]), .q17(R10_q31[14]), .d18(demultiplexer_2_out10[13]),
    .q18(R10_q31[13]), .d19(demultiplexer_2_out10[12]), .q19(R10_q31[12]), .d20(demultiplexer_2_out10[11]),
    .q20(R10_q31[11]), .d21(demultiplexer_2_out10[10]), .q21(R10_q31[10]), .d22(demultiplexer_2_out10[9]),
    .q22(R10_q31[9]), .d23(demultiplexer_2_out10[8]), .q23(R10_q31[8]), .d24(demultiplexer_2_out10[7]),
    .q24(R10_q31[7]), .d25(demultiplexer_2_out10[6]), .q25(R10_q31[6]), .d26(demultiplexer_2_out10[5]),
    .q26(R10_q31[5]), .d27(demultiplexer_2_out10[4]), .q27(R10_q31[4]), .d28(demultiplexer_2_out10[3]),
    .q28(R10_q31[3]), .d29(demultiplexer_2_out10[2]), .q29(R10_q31[2]), .d30(demultiplexer_2_out10[1]),
    .q30(R10_q31[1]), .d31(demultiplexer_2_out10[0]), .q31(R10_q31[0]));  // open: in, out, clr
  Shift_Register #(.length(32)) R11 (
    .shift(1'b0), .clk(Clock), .load(demultiplexer_1_out11), .d0(demultiplexer_2_out11[31]),
    .q0(R11_q31[31]), .d1(demultiplexer_2_out11[30]), .q1(R11_q31[30]), .d2(demultiplexer_2_out11[29]),
    .q2(R11_q31[29]), .d3(demultiplexer_2_out11[28]), .q3(R11_q31[28]), .d4(demultiplexer_2_out11[27]),
    .q4(R11_q31[27]), .d5(demultiplexer_2_out11[26]), .q5(R11_q31[26]), .d6(demultiplexer_2_out11[25]),
    .q6(R11_q31[25]), .d7(demultiplexer_2_out11[24]), .q7(R11_q31[24]), .d8(demultiplexer_2_out11[23]),
    .q8(R11_q31[23]), .d9(demultiplexer_2_out11[22]), .q9(R11_q31[22]), .d10(demultiplexer_2_out11[21]),
    .q10(R11_q31[21]), .d11(demultiplexer_2_out11[20]), .q11(R11_q31[20]), .d12(demultiplexer_2_out11[19]),
    .q12(R11_q31[19]), .d13(demultiplexer_2_out11[18]), .q13(R11_q31[18]), .d14(demultiplexer_2_out11[17]),
    .q14(R11_q31[17]), .d15(demultiplexer_2_out11[16]), .q15(R11_q31[16]), .d16(demultiplexer_2_out11[15]),
    .q16(R11_q31[15]), .d17(demultiplexer_2_out11[14]), .q17(R11_q31[14]), .d18(demultiplexer_2_out11[13]),
    .q18(R11_q31[13]), .d19(demultiplexer_2_out11[12]), .q19(R11_q31[12]), .d20(demultiplexer_2_out11[11]),
    .q20(R11_q31[11]), .d21(demultiplexer_2_out11[10]), .q21(R11_q31[10]), .d22(demultiplexer_2_out11[9]),
    .q22(R11_q31[9]), .d23(demultiplexer_2_out11[8]), .q23(R11_q31[8]), .d24(demultiplexer_2_out11[7]),
    .q24(R11_q31[7]), .d25(demultiplexer_2_out11[6]), .q25(R11_q31[6]), .d26(demultiplexer_2_out11[5]),
    .q26(R11_q31[5]), .d27(demultiplexer_2_out11[4]), .q27(R11_q31[4]), .d28(demultiplexer_2_out11[3]),
    .q28(R11_q31[3]), .d29(demultiplexer_2_out11[2]), .q29(R11_q31[2]), .d30(demultiplexer_2_out11[1]),
    .q30(R11_q31[1]), .d31(demultiplexer_2_out11[0]), .q31(R11_q31[0]));  // open: in, out, clr
  Shift_Register #(.length(32)) R12 (
    .shift(1'b0), .clk(Clock), .load(demultiplexer_1_out12), .d0(demultiplexer_2_out12[31]),
    .q0(R12_q31[31]), .d1(demultiplexer_2_out12[30]), .q1(R12_q31[30]), .d2(demultiplexer_2_out12[29]),
    .q2(R12_q31[29]), .d3(demultiplexer_2_out12[28]), .q3(R12_q31[28]), .d4(demultiplexer_2_out12[27]),
    .q4(R12_q31[27]), .d5(demultiplexer_2_out12[26]), .q5(R12_q31[26]), .d6(demultiplexer_2_out12[25]),
    .q6(R12_q31[25]), .d7(demultiplexer_2_out12[24]), .q7(R12_q31[24]), .d8(demultiplexer_2_out12[23]),
    .q8(R12_q31[23]), .d9(demultiplexer_2_out12[22]), .q9(R12_q31[22]), .d10(demultiplexer_2_out12[21]),
    .q10(R12_q31[21]), .d11(demultiplexer_2_out12[20]), .q11(R12_q31[20]), .d12(demultiplexer_2_out12[19]),
    .q12(R12_q31[19]), .d13(demultiplexer_2_out12[18]), .q13(R12_q31[18]), .d14(demultiplexer_2_out12[17]),
    .q14(R12_q31[17]), .d15(demultiplexer_2_out12[16]), .q15(R12_q31[16]), .d16(demultiplexer_2_out12[15]),
    .q16(R12_q31[15]), .d17(demultiplexer_2_out12[14]), .q17(R12_q31[14]), .d18(demultiplexer_2_out12[13]),
    .q18(R12_q31[13]), .d19(demultiplexer_2_out12[12]), .q19(R12_q31[12]), .d20(demultiplexer_2_out12[11]),
    .q20(R12_q31[11]), .d21(demultiplexer_2_out12[10]), .q21(R12_q31[10]), .d22(demultiplexer_2_out12[9]),
    .q22(R12_q31[9]), .d23(demultiplexer_2_out12[8]), .q23(R12_q31[8]), .d24(demultiplexer_2_out12[7]),
    .q24(R12_q31[7]), .d25(demultiplexer_2_out12[6]), .q25(R12_q31[6]), .d26(demultiplexer_2_out12[5]),
    .q26(R12_q31[5]), .d27(demultiplexer_2_out12[4]), .q27(R12_q31[4]), .d28(demultiplexer_2_out12[3]),
    .q28(R12_q31[3]), .d29(demultiplexer_2_out12[2]), .q29(R12_q31[2]), .d30(demultiplexer_2_out12[1]),
    .q30(R12_q31[1]), .d31(demultiplexer_2_out12[0]), .q31(R12_q31[0]));  // open: in, out, clr
  Shift_Register #(.length(32)) R13 (
    .shift(1'b0), .clk(Clock), .load(demultiplexer_1_out13), .d0(demultiplexer_2_out13[31]),
    .q0(R13_q31[31]), .d1(demultiplexer_2_out13[30]), .q1(R13_q31[30]), .d2(demultiplexer_2_out13[29]),
    .q2(R13_q31[29]), .d3(demultiplexer_2_out13[28]), .q3(R13_q31[28]), .d4(demultiplexer_2_out13[27]),
    .q4(R13_q31[27]), .d5(demultiplexer_2_out13[26]), .q5(R13_q31[26]), .d6(demultiplexer_2_out13[25]),
    .q6(R13_q31[25]), .d7(demultiplexer_2_out13[24]), .q7(R13_q31[24]), .d8(demultiplexer_2_out13[23]),
    .q8(R13_q31[23]), .d9(demultiplexer_2_out13[22]), .q9(R13_q31[22]), .d10(demultiplexer_2_out13[21]),
    .q10(R13_q31[21]), .d11(demultiplexer_2_out13[20]), .q11(R13_q31[20]), .d12(demultiplexer_2_out13[19]),
    .q12(R13_q31[19]), .d13(demultiplexer_2_out13[18]), .q13(R13_q31[18]), .d14(demultiplexer_2_out13[17]),
    .q14(R13_q31[17]), .d15(demultiplexer_2_out13[16]), .q15(R13_q31[16]), .d16(demultiplexer_2_out13[15]),
    .q16(R13_q31[15]), .d17(demultiplexer_2_out13[14]), .q17(R13_q31[14]), .d18(demultiplexer_2_out13[13]),
    .q18(R13_q31[13]), .d19(demultiplexer_2_out13[12]), .q19(R13_q31[12]), .d20(demultiplexer_2_out13[11]),
    .q20(R13_q31[11]), .d21(demultiplexer_2_out13[10]), .q21(R13_q31[10]), .d22(demultiplexer_2_out13[9]),
    .q22(R13_q31[9]), .d23(demultiplexer_2_out13[8]), .q23(R13_q31[8]), .d24(demultiplexer_2_out13[7]),
    .q24(R13_q31[7]), .d25(demultiplexer_2_out13[6]), .q25(R13_q31[6]), .d26(demultiplexer_2_out13[5]),
    .q26(R13_q31[5]), .d27(demultiplexer_2_out13[4]), .q27(R13_q31[4]), .d28(demultiplexer_2_out13[3]),
    .q28(R13_q31[3]), .d29(demultiplexer_2_out13[2]), .q29(R13_q31[2]), .d30(demultiplexer_2_out13[1]),
    .q30(R13_q31[1]), .d31(demultiplexer_2_out13[0]), .q31(R13_q31[0]));  // open: in, out, clr
  Shift_Register #(.length(32)) R14 (
    .shift(1'b0), .clk(Clock), .load(demultiplexer_1_out14), .d0(demultiplexer_2_out14[31]),
    .q0(R14_q31[31]), .d1(demultiplexer_2_out14[30]), .q1(R14_q31[30]), .d2(demultiplexer_2_out14[29]),
    .q2(R14_q31[29]), .d3(demultiplexer_2_out14[28]), .q3(R14_q31[28]), .d4(demultiplexer_2_out14[27]),
    .q4(R14_q31[27]), .d5(demultiplexer_2_out14[26]), .q5(R14_q31[26]), .d6(demultiplexer_2_out14[25]),
    .q6(R14_q31[25]), .d7(demultiplexer_2_out14[24]), .q7(R14_q31[24]), .d8(demultiplexer_2_out14[23]),
    .q8(R14_q31[23]), .d9(demultiplexer_2_out14[22]), .q9(R14_q31[22]), .d10(demultiplexer_2_out14[21]),
    .q10(R14_q31[21]), .d11(demultiplexer_2_out14[20]), .q11(R14_q31[20]), .d12(demultiplexer_2_out14[19]),
    .q12(R14_q31[19]), .d13(demultiplexer_2_out14[18]), .q13(R14_q31[18]), .d14(demultiplexer_2_out14[17]),
    .q14(R14_q31[17]), .d15(demultiplexer_2_out14[16]), .q15(R14_q31[16]), .d16(demultiplexer_2_out14[15]),
    .q16(R14_q31[15]), .d17(demultiplexer_2_out14[14]), .q17(R14_q31[14]), .d18(demultiplexer_2_out14[13]),
    .q18(R14_q31[13]), .d19(demultiplexer_2_out14[12]), .q19(R14_q31[12]), .d20(demultiplexer_2_out14[11]),
    .q20(R14_q31[11]), .d21(demultiplexer_2_out14[10]), .q21(R14_q31[10]), .d22(demultiplexer_2_out14[9]),
    .q22(R14_q31[9]), .d23(demultiplexer_2_out14[8]), .q23(R14_q31[8]), .d24(demultiplexer_2_out14[7]),
    .q24(R14_q31[7]), .d25(demultiplexer_2_out14[6]), .q25(R14_q31[6]), .d26(demultiplexer_2_out14[5]),
    .q26(R14_q31[5]), .d27(demultiplexer_2_out14[4]), .q27(R14_q31[4]), .d28(demultiplexer_2_out14[3]),
    .q28(R14_q31[3]), .d29(demultiplexer_2_out14[2]), .q29(R14_q31[2]), .d30(demultiplexer_2_out14[1]),
    .q30(R14_q31[1]), .d31(demultiplexer_2_out14[0]), .q31(R14_q31[0]));  // open: in, out, clr
  Shift_Register #(.length(32)) R15 (
    .shift(1'b0), .clk(Clock), .load(demultiplexer_1_out15), .d0(demultiplexer_2_out15[31]),
    .q0(R15_q31[31]), .d1(demultiplexer_2_out15[30]), .q1(R15_q31[30]), .d2(demultiplexer_2_out15[29]),
    .q2(R15_q31[29]), .d3(demultiplexer_2_out15[28]), .q3(R15_q31[28]), .d4(demultiplexer_2_out15[27]),
    .q4(R15_q31[27]), .d5(demultiplexer_2_out15[26]), .q5(R15_q31[26]), .d6(demultiplexer_2_out15[25]),
    .q6(R15_q31[25]), .d7(demultiplexer_2_out15[24]), .q7(R15_q31[24]), .d8(demultiplexer_2_out15[23]),
    .q8(R15_q31[23]), .d9(demultiplexer_2_out15[22]), .q9(R15_q31[22]), .d10(demultiplexer_2_out15[21]),
    .q10(R15_q31[21]), .d11(demultiplexer_2_out15[20]), .q11(R15_q31[20]), .d12(demultiplexer_2_out15[19]),
    .q12(R15_q31[19]), .d13(demultiplexer_2_out15[18]), .q13(R15_q31[18]), .d14(demultiplexer_2_out15[17]),
    .q14(R15_q31[17]), .d15(demultiplexer_2_out15[16]), .q15(R15_q31[16]), .d16(demultiplexer_2_out15[15]),
    .q16(R15_q31[15]), .d17(demultiplexer_2_out15[14]), .q17(R15_q31[14]), .d18(demultiplexer_2_out15[13]),
    .q18(R15_q31[13]), .d19(demultiplexer_2_out15[12]), .q19(R15_q31[12]), .d20(demultiplexer_2_out15[11]),
    .q20(R15_q31[11]), .d21(demultiplexer_2_out15[10]), .q21(R15_q31[10]), .d22(demultiplexer_2_out15[9]),
    .q22(R15_q31[9]), .d23(demultiplexer_2_out15[8]), .q23(R15_q31[8]), .d24(demultiplexer_2_out15[7]),
    .q24(R15_q31[7]), .d25(demultiplexer_2_out15[6]), .q25(R15_q31[6]), .d26(demultiplexer_2_out15[5]),
    .q26(R15_q31[5]), .d27(demultiplexer_2_out15[4]), .q27(R15_q31[4]), .d28(demultiplexer_2_out15[3]),
    .q28(R15_q31[3]), .d29(demultiplexer_2_out15[2]), .q29(R15_q31[2]), .d30(demultiplexer_2_out15[1]),
    .q30(R15_q31[1]), .d31(demultiplexer_2_out15[0]), .q31(R15_q31[0]));  // open: in, out, clr
  Shift_Register #(.length(32)) R16 (
    .shift(1'b0), .clk(Clock), .load(demultiplexer_1_out16), .d0(demultiplexer_2_out16[31]),
    .q0(R16_q31[31]), .d1(demultiplexer_2_out16[30]), .q1(R16_q31[30]), .d2(demultiplexer_2_out16[29]),
    .q2(R16_q31[29]), .d3(demultiplexer_2_out16[28]), .q3(R16_q31[28]), .d4(demultiplexer_2_out16[27]),
    .q4(R16_q31[27]), .d5(demultiplexer_2_out16[26]), .q5(R16_q31[26]), .d6(demultiplexer_2_out16[25]),
    .q6(R16_q31[25]), .d7(demultiplexer_2_out16[24]), .q7(R16_q31[24]), .d8(demultiplexer_2_out16[23]),
    .q8(R16_q31[23]), .d9(demultiplexer_2_out16[22]), .q9(R16_q31[22]), .d10(demultiplexer_2_out16[21]),
    .q10(R16_q31[21]), .d11(demultiplexer_2_out16[20]), .q11(R16_q31[20]), .d12(demultiplexer_2_out16[19]),
    .q12(R16_q31[19]), .d13(demultiplexer_2_out16[18]), .q13(R16_q31[18]), .d14(demultiplexer_2_out16[17]),
    .q14(R16_q31[17]), .d15(demultiplexer_2_out16[16]), .q15(R16_q31[16]), .d16(demultiplexer_2_out16[15]),
    .q16(R16_q31[15]), .d17(demultiplexer_2_out16[14]), .q17(R16_q31[14]), .d18(demultiplexer_2_out16[13]),
    .q18(R16_q31[13]), .d19(demultiplexer_2_out16[12]), .q19(R16_q31[12]), .d20(demultiplexer_2_out16[11]),
    .q20(R16_q31[11]), .d21(demultiplexer_2_out16[10]), .q21(R16_q31[10]), .d22(demultiplexer_2_out16[9]),
    .q22(R16_q31[9]), .d23(demultiplexer_2_out16[8]), .q23(R16_q31[8]), .d24(demultiplexer_2_out16[7]),
    .q24(R16_q31[7]), .d25(demultiplexer_2_out16[6]), .q25(R16_q31[6]), .d26(demultiplexer_2_out16[5]),
    .q26(R16_q31[5]), .d27(demultiplexer_2_out16[4]), .q27(R16_q31[4]), .d28(demultiplexer_2_out16[3]),
    .q28(R16_q31[3]), .d29(demultiplexer_2_out16[2]), .q29(R16_q31[2]), .d30(demultiplexer_2_out16[1]),
    .q30(R16_q31[1]), .d31(demultiplexer_2_out16[0]), .q31(R16_q31[0]));  // open: in, out, clr
  Shift_Register #(.length(32)) R17 (
    .shift(1'b0), .clk(Clock), .load(demultiplexer_1_out17), .d0(demultiplexer_2_out17[31]),
    .q0(R17_q31[31]), .d1(demultiplexer_2_out17[30]), .q1(R17_q31[30]), .d2(demultiplexer_2_out17[29]),
    .q2(R17_q31[29]), .d3(demultiplexer_2_out17[28]), .q3(R17_q31[28]), .d4(demultiplexer_2_out17[27]),
    .q4(R17_q31[27]), .d5(demultiplexer_2_out17[26]), .q5(R17_q31[26]), .d6(demultiplexer_2_out17[25]),
    .q6(R17_q31[25]), .d7(demultiplexer_2_out17[24]), .q7(R17_q31[24]), .d8(demultiplexer_2_out17[23]),
    .q8(R17_q31[23]), .d9(demultiplexer_2_out17[22]), .q9(R17_q31[22]), .d10(demultiplexer_2_out17[21]),
    .q10(R17_q31[21]), .d11(demultiplexer_2_out17[20]), .q11(R17_q31[20]), .d12(demultiplexer_2_out17[19]),
    .q12(R17_q31[19]), .d13(demultiplexer_2_out17[18]), .q13(R17_q31[18]), .d14(demultiplexer_2_out17[17]),
    .q14(R17_q31[17]), .d15(demultiplexer_2_out17[16]), .q15(R17_q31[16]), .d16(demultiplexer_2_out17[15]),
    .q16(R17_q31[15]), .d17(demultiplexer_2_out17[14]), .q17(R17_q31[14]), .d18(demultiplexer_2_out17[13]),
    .q18(R17_q31[13]), .d19(demultiplexer_2_out17[12]), .q19(R17_q31[12]), .d20(demultiplexer_2_out17[11]),
    .q20(R17_q31[11]), .d21(demultiplexer_2_out17[10]), .q21(R17_q31[10]), .d22(demultiplexer_2_out17[9]),
    .q22(R17_q31[9]), .d23(demultiplexer_2_out17[8]), .q23(R17_q31[8]), .d24(demultiplexer_2_out17[7]),
    .q24(R17_q31[7]), .d25(demultiplexer_2_out17[6]), .q25(R17_q31[6]), .d26(demultiplexer_2_out17[5]),
    .q26(R17_q31[5]), .d27(demultiplexer_2_out17[4]), .q27(R17_q31[4]), .d28(demultiplexer_2_out17[3]),
    .q28(R17_q31[3]), .d29(demultiplexer_2_out17[2]), .q29(R17_q31[2]), .d30(demultiplexer_2_out17[1]),
    .q30(R17_q31[1]), .d31(demultiplexer_2_out17[0]), .q31(R17_q31[0]));  // open: in, out, clr
  Shift_Register #(.length(32)) R18 (
    .shift(1'b0), .clk(Clock), .load(demultiplexer_1_out18), .d0(demultiplexer_2_out18[31]),
    .q0(R18_q31[31]), .d1(demultiplexer_2_out18[30]), .q1(R18_q31[30]), .d2(demultiplexer_2_out18[29]),
    .q2(R18_q31[29]), .d3(demultiplexer_2_out18[28]), .q3(R18_q31[28]), .d4(demultiplexer_2_out18[27]),
    .q4(R18_q31[27]), .d5(demultiplexer_2_out18[26]), .q5(R18_q31[26]), .d6(demultiplexer_2_out18[25]),
    .q6(R18_q31[25]), .d7(demultiplexer_2_out18[24]), .q7(R18_q31[24]), .d8(demultiplexer_2_out18[23]),
    .q8(R18_q31[23]), .d9(demultiplexer_2_out18[22]), .q9(R18_q31[22]), .d10(demultiplexer_2_out18[21]),
    .q10(R18_q31[21]), .d11(demultiplexer_2_out18[20]), .q11(R18_q31[20]), .d12(demultiplexer_2_out18[19]),
    .q12(R18_q31[19]), .d13(demultiplexer_2_out18[18]), .q13(R18_q31[18]), .d14(demultiplexer_2_out18[17]),
    .q14(R18_q31[17]), .d15(demultiplexer_2_out18[16]), .q15(R18_q31[16]), .d16(demultiplexer_2_out18[15]),
    .q16(R18_q31[15]), .d17(demultiplexer_2_out18[14]), .q17(R18_q31[14]), .d18(demultiplexer_2_out18[13]),
    .q18(R18_q31[13]), .d19(demultiplexer_2_out18[12]), .q19(R18_q31[12]), .d20(demultiplexer_2_out18[11]),
    .q20(R18_q31[11]), .d21(demultiplexer_2_out18[10]), .q21(R18_q31[10]), .d22(demultiplexer_2_out18[9]),
    .q22(R18_q31[9]), .d23(demultiplexer_2_out18[8]), .q23(R18_q31[8]), .d24(demultiplexer_2_out18[7]),
    .q24(R18_q31[7]), .d25(demultiplexer_2_out18[6]), .q25(R18_q31[6]), .d26(demultiplexer_2_out18[5]),
    .q26(R18_q31[5]), .d27(demultiplexer_2_out18[4]), .q27(R18_q31[4]), .d28(demultiplexer_2_out18[3]),
    .q28(R18_q31[3]), .d29(demultiplexer_2_out18[2]), .q29(R18_q31[2]), .d30(demultiplexer_2_out18[1]),
    .q30(R18_q31[1]), .d31(demultiplexer_2_out18[0]), .q31(R18_q31[0]));  // open: in, out, clr
  Shift_Register #(.length(32)) R19 (
    .shift(1'b0), .clk(Clock), .load(demultiplexer_1_out19), .d0(demultiplexer_2_out19[31]),
    .q0(R19_q31[31]), .d1(demultiplexer_2_out19[30]), .q1(R19_q31[30]), .d2(demultiplexer_2_out19[29]),
    .q2(R19_q31[29]), .d3(demultiplexer_2_out19[28]), .q3(R19_q31[28]), .d4(demultiplexer_2_out19[27]),
    .q4(R19_q31[27]), .d5(demultiplexer_2_out19[26]), .q5(R19_q31[26]), .d6(demultiplexer_2_out19[25]),
    .q6(R19_q31[25]), .d7(demultiplexer_2_out19[24]), .q7(R19_q31[24]), .d8(demultiplexer_2_out19[23]),
    .q8(R19_q31[23]), .d9(demultiplexer_2_out19[22]), .q9(R19_q31[22]), .d10(demultiplexer_2_out19[21]),
    .q10(R19_q31[21]), .d11(demultiplexer_2_out19[20]), .q11(R19_q31[20]), .d12(demultiplexer_2_out19[19]),
    .q12(R19_q31[19]), .d13(demultiplexer_2_out19[18]), .q13(R19_q31[18]), .d14(demultiplexer_2_out19[17]),
    .q14(R19_q31[17]), .d15(demultiplexer_2_out19[16]), .q15(R19_q31[16]), .d16(demultiplexer_2_out19[15]),
    .q16(R19_q31[15]), .d17(demultiplexer_2_out19[14]), .q17(R19_q31[14]), .d18(demultiplexer_2_out19[13]),
    .q18(R19_q31[13]), .d19(demultiplexer_2_out19[12]), .q19(R19_q31[12]), .d20(demultiplexer_2_out19[11]),
    .q20(R19_q31[11]), .d21(demultiplexer_2_out19[10]), .q21(R19_q31[10]), .d22(demultiplexer_2_out19[9]),
    .q22(R19_q31[9]), .d23(demultiplexer_2_out19[8]), .q23(R19_q31[8]), .d24(demultiplexer_2_out19[7]),
    .q24(R19_q31[7]), .d25(demultiplexer_2_out19[6]), .q25(R19_q31[6]), .d26(demultiplexer_2_out19[5]),
    .q26(R19_q31[5]), .d27(demultiplexer_2_out19[4]), .q27(R19_q31[4]), .d28(demultiplexer_2_out19[3]),
    .q28(R19_q31[3]), .d29(demultiplexer_2_out19[2]), .q29(R19_q31[2]), .d30(demultiplexer_2_out19[1]),
    .q30(R19_q31[1]), .d31(demultiplexer_2_out19[0]), .q31(R19_q31[0]));  // open: in, out, clr
  Shift_Register #(.length(32)) R20 (
    .shift(1'b0), .clk(Clock), .load(demultiplexer_1_out20), .d0(demultiplexer_2_out20[31]),
    .q0(R20_q31[31]), .d1(demultiplexer_2_out20[30]), .q1(R20_q31[30]), .d2(demultiplexer_2_out20[29]),
    .q2(R20_q31[29]), .d3(demultiplexer_2_out20[28]), .q3(R20_q31[28]), .d4(demultiplexer_2_out20[27]),
    .q4(R20_q31[27]), .d5(demultiplexer_2_out20[26]), .q5(R20_q31[26]), .d6(demultiplexer_2_out20[25]),
    .q6(R20_q31[25]), .d7(demultiplexer_2_out20[24]), .q7(R20_q31[24]), .d8(demultiplexer_2_out20[23]),
    .q8(R20_q31[23]), .d9(demultiplexer_2_out20[22]), .q9(R20_q31[22]), .d10(demultiplexer_2_out20[21]),
    .q10(R20_q31[21]), .d11(demultiplexer_2_out20[20]), .q11(R20_q31[20]), .d12(demultiplexer_2_out20[19]),
    .q12(R20_q31[19]), .d13(demultiplexer_2_out20[18]), .q13(R20_q31[18]), .d14(demultiplexer_2_out20[17]),
    .q14(R20_q31[17]), .d15(demultiplexer_2_out20[16]), .q15(R20_q31[16]), .d16(demultiplexer_2_out20[15]),
    .q16(R20_q31[15]), .d17(demultiplexer_2_out20[14]), .q17(R20_q31[14]), .d18(demultiplexer_2_out20[13]),
    .q18(R20_q31[13]), .d19(demultiplexer_2_out20[12]), .q19(R20_q31[12]), .d20(demultiplexer_2_out20[11]),
    .q20(R20_q31[11]), .d21(demultiplexer_2_out20[10]), .q21(R20_q31[10]), .d22(demultiplexer_2_out20[9]),
    .q22(R20_q31[9]), .d23(demultiplexer_2_out20[8]), .q23(R20_q31[8]), .d24(demultiplexer_2_out20[7]),
    .q24(R20_q31[7]), .d25(demultiplexer_2_out20[6]), .q25(R20_q31[6]), .d26(demultiplexer_2_out20[5]),
    .q26(R20_q31[5]), .d27(demultiplexer_2_out20[4]), .q27(R20_q31[4]), .d28(demultiplexer_2_out20[3]),
    .q28(R20_q31[3]), .d29(demultiplexer_2_out20[2]), .q29(R20_q31[2]), .d30(demultiplexer_2_out20[1]),
    .q30(R20_q31[1]), .d31(demultiplexer_2_out20[0]), .q31(R20_q31[0]));  // open: in, out, clr
  Shift_Register #(.length(32)) R21 (
    .shift(1'b0), .clk(Clock), .load(demultiplexer_1_out21), .d0(demultiplexer_2_out21[31]),
    .q0(R21_q31[31]), .d1(demultiplexer_2_out21[30]), .q1(R21_q31[30]), .d2(demultiplexer_2_out21[29]),
    .q2(R21_q31[29]), .d3(demultiplexer_2_out21[28]), .q3(R21_q31[28]), .d4(demultiplexer_2_out21[27]),
    .q4(R21_q31[27]), .d5(demultiplexer_2_out21[26]), .q5(R21_q31[26]), .d6(demultiplexer_2_out21[25]),
    .q6(R21_q31[25]), .d7(demultiplexer_2_out21[24]), .q7(R21_q31[24]), .d8(demultiplexer_2_out21[23]),
    .q8(R21_q31[23]), .d9(demultiplexer_2_out21[22]), .q9(R21_q31[22]), .d10(demultiplexer_2_out21[21]),
    .q10(R21_q31[21]), .d11(demultiplexer_2_out21[20]), .q11(R21_q31[20]), .d12(demultiplexer_2_out21[19]),
    .q12(R21_q31[19]), .d13(demultiplexer_2_out21[18]), .q13(R21_q31[18]), .d14(demultiplexer_2_out21[17]),
    .q14(R21_q31[17]), .d15(demultiplexer_2_out21[16]), .q15(R21_q31[16]), .d16(demultiplexer_2_out21[15]),
    .q16(R21_q31[15]), .d17(demultiplexer_2_out21[14]), .q17(R21_q31[14]), .d18(demultiplexer_2_out21[13]),
    .q18(R21_q31[13]), .d19(demultiplexer_2_out21[12]), .q19(R21_q31[12]), .d20(demultiplexer_2_out21[11]),
    .q20(R21_q31[11]), .d21(demultiplexer_2_out21[10]), .q21(R21_q31[10]), .d22(demultiplexer_2_out21[9]),
    .q22(R21_q31[9]), .d23(demultiplexer_2_out21[8]), .q23(R21_q31[8]), .d24(demultiplexer_2_out21[7]),
    .q24(R21_q31[7]), .d25(demultiplexer_2_out21[6]), .q25(R21_q31[6]), .d26(demultiplexer_2_out21[5]),
    .q26(R21_q31[5]), .d27(demultiplexer_2_out21[4]), .q27(R21_q31[4]), .d28(demultiplexer_2_out21[3]),
    .q28(R21_q31[3]), .d29(demultiplexer_2_out21[2]), .q29(R21_q31[2]), .d30(demultiplexer_2_out21[1]),
    .q30(R21_q31[1]), .d31(demultiplexer_2_out21[0]), .q31(R21_q31[0]));  // open: in, out, clr
  Shift_Register #(.length(32)) R22 (
    .shift(1'b0), .clk(Clock), .load(demultiplexer_1_out22), .d0(demultiplexer_2_out22[31]),
    .q0(R22_q31[31]), .d1(demultiplexer_2_out22[30]), .q1(R22_q31[30]), .d2(demultiplexer_2_out22[29]),
    .q2(R22_q31[29]), .d3(demultiplexer_2_out22[28]), .q3(R22_q31[28]), .d4(demultiplexer_2_out22[27]),
    .q4(R22_q31[27]), .d5(demultiplexer_2_out22[26]), .q5(R22_q31[26]), .d6(demultiplexer_2_out22[25]),
    .q6(R22_q31[25]), .d7(demultiplexer_2_out22[24]), .q7(R22_q31[24]), .d8(demultiplexer_2_out22[23]),
    .q8(R22_q31[23]), .d9(demultiplexer_2_out22[22]), .q9(R22_q31[22]), .d10(demultiplexer_2_out22[21]),
    .q10(R22_q31[21]), .d11(demultiplexer_2_out22[20]), .q11(R22_q31[20]), .d12(demultiplexer_2_out22[19]),
    .q12(R22_q31[19]), .d13(demultiplexer_2_out22[18]), .q13(R22_q31[18]), .d14(demultiplexer_2_out22[17]),
    .q14(R22_q31[17]), .d15(demultiplexer_2_out22[16]), .q15(R22_q31[16]), .d16(demultiplexer_2_out22[15]),
    .q16(R22_q31[15]), .d17(demultiplexer_2_out22[14]), .q17(R22_q31[14]), .d18(demultiplexer_2_out22[13]),
    .q18(R22_q31[13]), .d19(demultiplexer_2_out22[12]), .q19(R22_q31[12]), .d20(demultiplexer_2_out22[11]),
    .q20(R22_q31[11]), .d21(demultiplexer_2_out22[10]), .q21(R22_q31[10]), .d22(demultiplexer_2_out22[9]),
    .q22(R22_q31[9]), .d23(demultiplexer_2_out22[8]), .q23(R22_q31[8]), .d24(demultiplexer_2_out22[7]),
    .q24(R22_q31[7]), .d25(demultiplexer_2_out22[6]), .q25(R22_q31[6]), .d26(demultiplexer_2_out22[5]),
    .q26(R22_q31[5]), .d27(demultiplexer_2_out22[4]), .q27(R22_q31[4]), .d28(demultiplexer_2_out22[3]),
    .q28(R22_q31[3]), .d29(demultiplexer_2_out22[2]), .q29(R22_q31[2]), .d30(demultiplexer_2_out22[1]),
    .q30(R22_q31[1]), .d31(demultiplexer_2_out22[0]), .q31(R22_q31[0]));  // open: in, out, clr
  Shift_Register #(.length(32)) R23 (
    .shift(1'b0), .clk(Clock), .load(demultiplexer_1_out23), .d0(demultiplexer_2_out23[31]),
    .q0(R23_q31[31]), .d1(demultiplexer_2_out23[30]), .q1(R23_q31[30]), .d2(demultiplexer_2_out23[29]),
    .q2(R23_q31[29]), .d3(demultiplexer_2_out23[28]), .q3(R23_q31[28]), .d4(demultiplexer_2_out23[27]),
    .q4(R23_q31[27]), .d5(demultiplexer_2_out23[26]), .q5(R23_q31[26]), .d6(demultiplexer_2_out23[25]),
    .q6(R23_q31[25]), .d7(demultiplexer_2_out23[24]), .q7(R23_q31[24]), .d8(demultiplexer_2_out23[23]),
    .q8(R23_q31[23]), .d9(demultiplexer_2_out23[22]), .q9(R23_q31[22]), .d10(demultiplexer_2_out23[21]),
    .q10(R23_q31[21]), .d11(demultiplexer_2_out23[20]), .q11(R23_q31[20]), .d12(demultiplexer_2_out23[19]),
    .q12(R23_q31[19]), .d13(demultiplexer_2_out23[18]), .q13(R23_q31[18]), .d14(demultiplexer_2_out23[17]),
    .q14(R23_q31[17]), .d15(demultiplexer_2_out23[16]), .q15(R23_q31[16]), .d16(demultiplexer_2_out23[15]),
    .q16(R23_q31[15]), .d17(demultiplexer_2_out23[14]), .q17(R23_q31[14]), .d18(demultiplexer_2_out23[13]),
    .q18(R23_q31[13]), .d19(demultiplexer_2_out23[12]), .q19(R23_q31[12]), .d20(demultiplexer_2_out23[11]),
    .q20(R23_q31[11]), .d21(demultiplexer_2_out23[10]), .q21(R23_q31[10]), .d22(demultiplexer_2_out23[9]),
    .q22(R23_q31[9]), .d23(demultiplexer_2_out23[8]), .q23(R23_q31[8]), .d24(demultiplexer_2_out23[7]),
    .q24(R23_q31[7]), .d25(demultiplexer_2_out23[6]), .q25(R23_q31[6]), .d26(demultiplexer_2_out23[5]),
    .q26(R23_q31[5]), .d27(demultiplexer_2_out23[4]), .q27(R23_q31[4]), .d28(demultiplexer_2_out23[3]),
    .q28(R23_q31[3]), .d29(demultiplexer_2_out23[2]), .q29(R23_q31[2]), .d30(demultiplexer_2_out23[1]),
    .q30(R23_q31[1]), .d31(demultiplexer_2_out23[0]), .q31(R23_q31[0]));  // open: in, out, clr
  Shift_Register #(.length(32)) R24 (
    .shift(1'b0), .clk(Clock), .load(demultiplexer_1_out24), .d0(demultiplexer_2_out24[31]),
    .q0(R24_q31[31]), .d1(demultiplexer_2_out24[30]), .q1(R24_q31[30]), .d2(demultiplexer_2_out24[29]),
    .q2(R24_q31[29]), .d3(demultiplexer_2_out24[28]), .q3(R24_q31[28]), .d4(demultiplexer_2_out24[27]),
    .q4(R24_q31[27]), .d5(demultiplexer_2_out24[26]), .q5(R24_q31[26]), .d6(demultiplexer_2_out24[25]),
    .q6(R24_q31[25]), .d7(demultiplexer_2_out24[24]), .q7(R24_q31[24]), .d8(demultiplexer_2_out24[23]),
    .q8(R24_q31[23]), .d9(demultiplexer_2_out24[22]), .q9(R24_q31[22]), .d10(demultiplexer_2_out24[21]),
    .q10(R24_q31[21]), .d11(demultiplexer_2_out24[20]), .q11(R24_q31[20]), .d12(demultiplexer_2_out24[19]),
    .q12(R24_q31[19]), .d13(demultiplexer_2_out24[18]), .q13(R24_q31[18]), .d14(demultiplexer_2_out24[17]),
    .q14(R24_q31[17]), .d15(demultiplexer_2_out24[16]), .q15(R24_q31[16]), .d16(demultiplexer_2_out24[15]),
    .q16(R24_q31[15]), .d17(demultiplexer_2_out24[14]), .q17(R24_q31[14]), .d18(demultiplexer_2_out24[13]),
    .q18(R24_q31[13]), .d19(demultiplexer_2_out24[12]), .q19(R24_q31[12]), .d20(demultiplexer_2_out24[11]),
    .q20(R24_q31[11]), .d21(demultiplexer_2_out24[10]), .q21(R24_q31[10]), .d22(demultiplexer_2_out24[9]),
    .q22(R24_q31[9]), .d23(demultiplexer_2_out24[8]), .q23(R24_q31[8]), .d24(demultiplexer_2_out24[7]),
    .q24(R24_q31[7]), .d25(demultiplexer_2_out24[6]), .q25(R24_q31[6]), .d26(demultiplexer_2_out24[5]),
    .q26(R24_q31[5]), .d27(demultiplexer_2_out24[4]), .q27(R24_q31[4]), .d28(demultiplexer_2_out24[3]),
    .q28(R24_q31[3]), .d29(demultiplexer_2_out24[2]), .q29(R24_q31[2]), .d30(demultiplexer_2_out24[1]),
    .q30(R24_q31[1]), .d31(demultiplexer_2_out24[0]), .q31(R24_q31[0]));  // open: in, out, clr
  Shift_Register #(.length(32)) R25 (
    .shift(1'b0), .clk(Clock), .load(demultiplexer_1_out25), .d0(demultiplexer_2_out25[31]),
    .q0(R25_q31[31]), .d1(demultiplexer_2_out25[30]), .q1(R25_q31[30]), .d2(demultiplexer_2_out25[29]),
    .q2(R25_q31[29]), .d3(demultiplexer_2_out25[28]), .q3(R25_q31[28]), .d4(demultiplexer_2_out25[27]),
    .q4(R25_q31[27]), .d5(demultiplexer_2_out25[26]), .q5(R25_q31[26]), .d6(demultiplexer_2_out25[25]),
    .q6(R25_q31[25]), .d7(demultiplexer_2_out25[24]), .q7(R25_q31[24]), .d8(demultiplexer_2_out25[23]),
    .q8(R25_q31[23]), .d9(demultiplexer_2_out25[22]), .q9(R25_q31[22]), .d10(demultiplexer_2_out25[21]),
    .q10(R25_q31[21]), .d11(demultiplexer_2_out25[20]), .q11(R25_q31[20]), .d12(demultiplexer_2_out25[19]),
    .q12(R25_q31[19]), .d13(demultiplexer_2_out25[18]), .q13(R25_q31[18]), .d14(demultiplexer_2_out25[17]),
    .q14(R25_q31[17]), .d15(demultiplexer_2_out25[16]), .q15(R25_q31[16]), .d16(demultiplexer_2_out25[15]),
    .q16(R25_q31[15]), .d17(demultiplexer_2_out25[14]), .q17(R25_q31[14]), .d18(demultiplexer_2_out25[13]),
    .q18(R25_q31[13]), .d19(demultiplexer_2_out25[12]), .q19(R25_q31[12]), .d20(demultiplexer_2_out25[11]),
    .q20(R25_q31[11]), .d21(demultiplexer_2_out25[10]), .q21(R25_q31[10]), .d22(demultiplexer_2_out25[9]),
    .q22(R25_q31[9]), .d23(demultiplexer_2_out25[8]), .q23(R25_q31[8]), .d24(demultiplexer_2_out25[7]),
    .q24(R25_q31[7]), .d25(demultiplexer_2_out25[6]), .q25(R25_q31[6]), .d26(demultiplexer_2_out25[5]),
    .q26(R25_q31[5]), .d27(demultiplexer_2_out25[4]), .q27(R25_q31[4]), .d28(demultiplexer_2_out25[3]),
    .q28(R25_q31[3]), .d29(demultiplexer_2_out25[2]), .q29(R25_q31[2]), .d30(demultiplexer_2_out25[1]),
    .q30(R25_q31[1]), .d31(demultiplexer_2_out25[0]), .q31(R25_q31[0]));  // open: in, out, clr
  Shift_Register #(.length(32)) R26 (
    .shift(1'b0), .clk(Clock), .load(demultiplexer_1_out26), .d0(demultiplexer_2_out26[31]),
    .q0(R26_q31[31]), .d1(demultiplexer_2_out26[30]), .q1(R26_q31[30]), .d2(demultiplexer_2_out26[29]),
    .q2(R26_q31[29]), .d3(demultiplexer_2_out26[28]), .q3(R26_q31[28]), .d4(demultiplexer_2_out26[27]),
    .q4(R26_q31[27]), .d5(demultiplexer_2_out26[26]), .q5(R26_q31[26]), .d6(demultiplexer_2_out26[25]),
    .q6(R26_q31[25]), .d7(demultiplexer_2_out26[24]), .q7(R26_q31[24]), .d8(demultiplexer_2_out26[23]),
    .q8(R26_q31[23]), .d9(demultiplexer_2_out26[22]), .q9(R26_q31[22]), .d10(demultiplexer_2_out26[21]),
    .q10(R26_q31[21]), .d11(demultiplexer_2_out26[20]), .q11(R26_q31[20]), .d12(demultiplexer_2_out26[19]),
    .q12(R26_q31[19]), .d13(demultiplexer_2_out26[18]), .q13(R26_q31[18]), .d14(demultiplexer_2_out26[17]),
    .q14(R26_q31[17]), .d15(demultiplexer_2_out26[16]), .q15(R26_q31[16]), .d16(demultiplexer_2_out26[15]),
    .q16(R26_q31[15]), .d17(demultiplexer_2_out26[14]), .q17(R26_q31[14]), .d18(demultiplexer_2_out26[13]),
    .q18(R26_q31[13]), .d19(demultiplexer_2_out26[12]), .q19(R26_q31[12]), .d20(demultiplexer_2_out26[11]),
    .q20(R26_q31[11]), .d21(demultiplexer_2_out26[10]), .q21(R26_q31[10]), .d22(demultiplexer_2_out26[9]),
    .q22(R26_q31[9]), .d23(demultiplexer_2_out26[8]), .q23(R26_q31[8]), .d24(demultiplexer_2_out26[7]),
    .q24(R26_q31[7]), .d25(demultiplexer_2_out26[6]), .q25(R26_q31[6]), .d26(demultiplexer_2_out26[5]),
    .q26(R26_q31[5]), .d27(demultiplexer_2_out26[4]), .q27(R26_q31[4]), .d28(demultiplexer_2_out26[3]),
    .q28(R26_q31[3]), .d29(demultiplexer_2_out26[2]), .q29(R26_q31[2]), .d30(demultiplexer_2_out26[1]),
    .q30(R26_q31[1]), .d31(demultiplexer_2_out26[0]), .q31(R26_q31[0]));  // open: in, out, clr
  Shift_Register #(.length(32)) R27 (
    .shift(1'b0), .clk(Clock), .load(demultiplexer_1_out27), .d0(demultiplexer_2_out27[31]),
    .q0(R27_q31[31]), .d1(demultiplexer_2_out27[30]), .q1(R27_q31[30]), .d2(demultiplexer_2_out27[29]),
    .q2(R27_q31[29]), .d3(demultiplexer_2_out27[28]), .q3(R27_q31[28]), .d4(demultiplexer_2_out27[27]),
    .q4(R27_q31[27]), .d5(demultiplexer_2_out27[26]), .q5(R27_q31[26]), .d6(demultiplexer_2_out27[25]),
    .q6(R27_q31[25]), .d7(demultiplexer_2_out27[24]), .q7(R27_q31[24]), .d8(demultiplexer_2_out27[23]),
    .q8(R27_q31[23]), .d9(demultiplexer_2_out27[22]), .q9(R27_q31[22]), .d10(demultiplexer_2_out27[21]),
    .q10(R27_q31[21]), .d11(demultiplexer_2_out27[20]), .q11(R27_q31[20]), .d12(demultiplexer_2_out27[19]),
    .q12(R27_q31[19]), .d13(demultiplexer_2_out27[18]), .q13(R27_q31[18]), .d14(demultiplexer_2_out27[17]),
    .q14(R27_q31[17]), .d15(demultiplexer_2_out27[16]), .q15(R27_q31[16]), .d16(demultiplexer_2_out27[15]),
    .q16(R27_q31[15]), .d17(demultiplexer_2_out27[14]), .q17(R27_q31[14]), .d18(demultiplexer_2_out27[13]),
    .q18(R27_q31[13]), .d19(demultiplexer_2_out27[12]), .q19(R27_q31[12]), .d20(demultiplexer_2_out27[11]),
    .q20(R27_q31[11]), .d21(demultiplexer_2_out27[10]), .q21(R27_q31[10]), .d22(demultiplexer_2_out27[9]),
    .q22(R27_q31[9]), .d23(demultiplexer_2_out27[8]), .q23(R27_q31[8]), .d24(demultiplexer_2_out27[7]),
    .q24(R27_q31[7]), .d25(demultiplexer_2_out27[6]), .q25(R27_q31[6]), .d26(demultiplexer_2_out27[5]),
    .q26(R27_q31[5]), .d27(demultiplexer_2_out27[4]), .q27(R27_q31[4]), .d28(demultiplexer_2_out27[3]),
    .q28(R27_q31[3]), .d29(demultiplexer_2_out27[2]), .q29(R27_q31[2]), .d30(demultiplexer_2_out27[1]),
    .q30(R27_q31[1]), .d31(demultiplexer_2_out27[0]), .q31(R27_q31[0]));  // open: in, out, clr
  Shift_Register #(.length(32)) R28 (
    .shift(1'b0), .clk(Clock), .load(demultiplexer_1_out28), .d0(demultiplexer_2_out28[31]),
    .q0(R28_q31[31]), .d1(demultiplexer_2_out28[30]), .q1(R28_q31[30]), .d2(demultiplexer_2_out28[29]),
    .q2(R28_q31[29]), .d3(demultiplexer_2_out28[28]), .q3(R28_q31[28]), .d4(demultiplexer_2_out28[27]),
    .q4(R28_q31[27]), .d5(demultiplexer_2_out28[26]), .q5(R28_q31[26]), .d6(demultiplexer_2_out28[25]),
    .q6(R28_q31[25]), .d7(demultiplexer_2_out28[24]), .q7(R28_q31[24]), .d8(demultiplexer_2_out28[23]),
    .q8(R28_q31[23]), .d9(demultiplexer_2_out28[22]), .q9(R28_q31[22]), .d10(demultiplexer_2_out28[21]),
    .q10(R28_q31[21]), .d11(demultiplexer_2_out28[20]), .q11(R28_q31[20]), .d12(demultiplexer_2_out28[19]),
    .q12(R28_q31[19]), .d13(demultiplexer_2_out28[18]), .q13(R28_q31[18]), .d14(demultiplexer_2_out28[17]),
    .q14(R28_q31[17]), .d15(demultiplexer_2_out28[16]), .q15(R28_q31[16]), .d16(demultiplexer_2_out28[15]),
    .q16(R28_q31[15]), .d17(demultiplexer_2_out28[14]), .q17(R28_q31[14]), .d18(demultiplexer_2_out28[13]),
    .q18(R28_q31[13]), .d19(demultiplexer_2_out28[12]), .q19(R28_q31[12]), .d20(demultiplexer_2_out28[11]),
    .q20(R28_q31[11]), .d21(demultiplexer_2_out28[10]), .q21(R28_q31[10]), .d22(demultiplexer_2_out28[9]),
    .q22(R28_q31[9]), .d23(demultiplexer_2_out28[8]), .q23(R28_q31[8]), .d24(demultiplexer_2_out28[7]),
    .q24(R28_q31[7]), .d25(demultiplexer_2_out28[6]), .q25(R28_q31[6]), .d26(demultiplexer_2_out28[5]),
    .q26(R28_q31[5]), .d27(demultiplexer_2_out28[4]), .q27(R28_q31[4]), .d28(demultiplexer_2_out28[3]),
    .q28(R28_q31[3]), .d29(demultiplexer_2_out28[2]), .q29(R28_q31[2]), .d30(demultiplexer_2_out28[1]),
    .q30(R28_q31[1]), .d31(demultiplexer_2_out28[0]), .q31(R28_q31[0]));  // open: in, out, clr
  Shift_Register #(.length(32)) R29 (
    .shift(1'b0), .clk(Clock), .load(demultiplexer_1_out29), .d0(demultiplexer_2_out29[31]),
    .q0(R29_q31[31]), .d1(demultiplexer_2_out29[30]), .q1(R29_q31[30]), .d2(demultiplexer_2_out29[29]),
    .q2(R29_q31[29]), .d3(demultiplexer_2_out29[28]), .q3(R29_q31[28]), .d4(demultiplexer_2_out29[27]),
    .q4(R29_q31[27]), .d5(demultiplexer_2_out29[26]), .q5(R29_q31[26]), .d6(demultiplexer_2_out29[25]),
    .q6(R29_q31[25]), .d7(demultiplexer_2_out29[24]), .q7(R29_q31[24]), .d8(demultiplexer_2_out29[23]),
    .q8(R29_q31[23]), .d9(demultiplexer_2_out29[22]), .q9(R29_q31[22]), .d10(demultiplexer_2_out29[21]),
    .q10(R29_q31[21]), .d11(demultiplexer_2_out29[20]), .q11(R29_q31[20]), .d12(demultiplexer_2_out29[19]),
    .q12(R29_q31[19]), .d13(demultiplexer_2_out29[18]), .q13(R29_q31[18]), .d14(demultiplexer_2_out29[17]),
    .q14(R29_q31[17]), .d15(demultiplexer_2_out29[16]), .q15(R29_q31[16]), .d16(demultiplexer_2_out29[15]),
    .q16(R29_q31[15]), .d17(demultiplexer_2_out29[14]), .q17(R29_q31[14]), .d18(demultiplexer_2_out29[13]),
    .q18(R29_q31[13]), .d19(demultiplexer_2_out29[12]), .q19(R29_q31[12]), .d20(demultiplexer_2_out29[11]),
    .q20(R29_q31[11]), .d21(demultiplexer_2_out29[10]), .q21(R29_q31[10]), .d22(demultiplexer_2_out29[9]),
    .q22(R29_q31[9]), .d23(demultiplexer_2_out29[8]), .q23(R29_q31[8]), .d24(demultiplexer_2_out29[7]),
    .q24(R29_q31[7]), .d25(demultiplexer_2_out29[6]), .q25(R29_q31[6]), .d26(demultiplexer_2_out29[5]),
    .q26(R29_q31[5]), .d27(demultiplexer_2_out29[4]), .q27(R29_q31[4]), .d28(demultiplexer_2_out29[3]),
    .q28(R29_q31[3]), .d29(demultiplexer_2_out29[2]), .q29(R29_q31[2]), .d30(demultiplexer_2_out29[1]),
    .q30(R29_q31[1]), .d31(demultiplexer_2_out29[0]), .q31(R29_q31[0]));  // open: in, out, clr
  Shift_Register #(.length(32)) R30 (
    .shift(1'b0), .clk(Clock), .load(demultiplexer_1_out30), .d0(demultiplexer_2_out30[31]),
    .q0(R30_q31[31]), .d1(demultiplexer_2_out30[30]), .q1(R30_q31[30]), .d2(demultiplexer_2_out30[29]),
    .q2(R30_q31[29]), .d3(demultiplexer_2_out30[28]), .q3(R30_q31[28]), .d4(demultiplexer_2_out30[27]),
    .q4(R30_q31[27]), .d5(demultiplexer_2_out30[26]), .q5(R30_q31[26]), .d6(demultiplexer_2_out30[25]),
    .q6(R30_q31[25]), .d7(demultiplexer_2_out30[24]), .q7(R30_q31[24]), .d8(demultiplexer_2_out30[23]),
    .q8(R30_q31[23]), .d9(demultiplexer_2_out30[22]), .q9(R30_q31[22]), .d10(demultiplexer_2_out30[21]),
    .q10(R30_q31[21]), .d11(demultiplexer_2_out30[20]), .q11(R30_q31[20]), .d12(demultiplexer_2_out30[19]),
    .q12(R30_q31[19]), .d13(demultiplexer_2_out30[18]), .q13(R30_q31[18]), .d14(demultiplexer_2_out30[17]),
    .q14(R30_q31[17]), .d15(demultiplexer_2_out30[16]), .q15(R30_q31[16]), .d16(demultiplexer_2_out30[15]),
    .q16(R30_q31[15]), .d17(demultiplexer_2_out30[14]), .q17(R30_q31[14]), .d18(demultiplexer_2_out30[13]),
    .q18(R30_q31[13]), .d19(demultiplexer_2_out30[12]), .q19(R30_q31[12]), .d20(demultiplexer_2_out30[11]),
    .q20(R30_q31[11]), .d21(demultiplexer_2_out30[10]), .q21(R30_q31[10]), .d22(demultiplexer_2_out30[9]),
    .q22(R30_q31[9]), .d23(demultiplexer_2_out30[8]), .q23(R30_q31[8]), .d24(demultiplexer_2_out30[7]),
    .q24(R30_q31[7]), .d25(demultiplexer_2_out30[6]), .q25(R30_q31[6]), .d26(demultiplexer_2_out30[5]),
    .q26(R30_q31[5]), .d27(demultiplexer_2_out30[4]), .q27(R30_q31[4]), .d28(demultiplexer_2_out30[3]),
    .q28(R30_q31[3]), .d29(demultiplexer_2_out30[2]), .q29(R30_q31[2]), .d30(demultiplexer_2_out30[1]),
    .q30(R30_q31[1]), .d31(demultiplexer_2_out30[0]), .q31(R30_q31[0]));  // open: in, out, clr
  Shift_Register #(.length(32)) R31 (
    .shift(1'b0), .clk(Clock), .load(demultiplexer_1_out31), .d0(demultiplexer_2_out31[31]),
    .q0(R31_q31[31]), .d1(demultiplexer_2_out31[30]), .q1(R31_q31[30]), .d2(demultiplexer_2_out31[29]),
    .q2(R31_q31[29]), .d3(demultiplexer_2_out31[28]), .q3(R31_q31[28]), .d4(demultiplexer_2_out31[27]),
    .q4(R31_q31[27]), .d5(demultiplexer_2_out31[26]), .q5(R31_q31[26]), .d6(demultiplexer_2_out31[25]),
    .q6(R31_q31[25]), .d7(demultiplexer_2_out31[24]), .q7(R31_q31[24]), .d8(demultiplexer_2_out31[23]),
    .q8(R31_q31[23]), .d9(demultiplexer_2_out31[22]), .q9(R31_q31[22]), .d10(demultiplexer_2_out31[21]),
    .q10(R31_q31[21]), .d11(demultiplexer_2_out31[20]), .q11(R31_q31[20]), .d12(demultiplexer_2_out31[19]),
    .q12(R31_q31[19]), .d13(demultiplexer_2_out31[18]), .q13(R31_q31[18]), .d14(demultiplexer_2_out31[17]),
    .q14(R31_q31[17]), .d15(demultiplexer_2_out31[16]), .q15(R31_q31[16]), .d16(demultiplexer_2_out31[15]),
    .q16(R31_q31[15]), .d17(demultiplexer_2_out31[14]), .q17(R31_q31[14]), .d18(demultiplexer_2_out31[13]),
    .q18(R31_q31[13]), .d19(demultiplexer_2_out31[12]), .q19(R31_q31[12]), .d20(demultiplexer_2_out31[11]),
    .q20(R31_q31[11]), .d21(demultiplexer_2_out31[10]), .q21(R31_q31[10]), .d22(demultiplexer_2_out31[9]),
    .q22(R31_q31[9]), .d23(demultiplexer_2_out31[8]), .q23(R31_q31[8]), .d24(demultiplexer_2_out31[7]),
    .q24(R31_q31[7]), .d25(demultiplexer_2_out31[6]), .q25(R31_q31[6]), .d26(demultiplexer_2_out31[5]),
    .q26(R31_q31[5]), .d27(demultiplexer_2_out31[4]), .q27(R31_q31[4]), .d28(demultiplexer_2_out31[3]),
    .q28(R31_q31[3]), .d29(demultiplexer_2_out31[2]), .q29(R31_q31[2]), .d30(demultiplexer_2_out31[1]),
    .q30(R31_q31[1]), .d31(demultiplexer_2_out31[0]), .q31(R31_q31[0]));  // open: in, out, clr
  Multiplexer #(.select(5), .width(32), .enable("false")) multiplexer_2 (
    .in0(R0_q31), .in1(R1_q31), .in2(R2_q31), .in3(R3_q31), .in4(R4_q31), .in5(R5_q31), .in6(R6_q31),
    .in7(R7_q31), .in8(R8_q31), .in9(R9_q31), .in10(R10_q31), .in11(R11_q31), .in12(R12_q31), .in13(R13_q31),
    .in14(R14_q31), .in15(R15_q31), .in16(R16_q31), .in17(R17_q31), .in18(R18_q31), .in19(R19_q31),
    .in20(R20_q31), .in21(R21_q31), .in22(R22_q31), .in23(R23_q31), .in24(R24_q31), .in25(R25_q31),
    .in26(R26_q31), .in27(R27_q31), .in28(R28_q31), .in29(R29_q31), .in30(R30_q31), .in31(R31_q31),
    .out(A_value), .sel(Add_A));
  Multiplexer #(.select(5), .width(32), .enable("false")) multiplexer_3 (
    .in0(R0_q31), .in1(R1_q31), .in2(R2_q31), .in3(R3_q31), .in4(R4_q31), .in5(R5_q31), .in6(R6_q31),
    .in7(R7_q31), .in8(R8_q31), .in9(R9_q31), .in10(R10_q31), .in11(R11_q31), .in12(R12_q31), .in13(R13_q31),
    .in14(R14_q31), .in15(R15_q31), .in16(R16_q31), .in17(R17_q31), .in18(R18_q31), .in19(R19_q31),
    .in20(R20_q31), .in21(R21_q31), .in22(R22_q31), .in23(R23_q31), .in24(R24_q31), .in25(R25_q31),
    .in26(R26_q31), .in27(R27_q31), .in28(R28_q31), .in29(R29_q31), .in30(R30_q31), .in31(R31_q31),
    .out(B_value), .sel(Add_B));
  Demultiplexer #(.select(5), .width(32)) demultiplexer_2 (
    .out0(demultiplexer_2_out0), .out1(demultiplexer_2_out1), .out2(demultiplexer_2_out2),
    .out3(demultiplexer_2_out3), .out4(demultiplexer_2_out4), .out5(demultiplexer_2_out5),
    .out6(demultiplexer_2_out6), .out7(demultiplexer_2_out7), .out8(demultiplexer_2_out8),
    .out9(demultiplexer_2_out9), .out10(demultiplexer_2_out10), .out11(demultiplexer_2_out11),
    .out12(demultiplexer_2_out12), .out13(demultiplexer_2_out13), .out14(demultiplexer_2_out14),
    .out15(demultiplexer_2_out15), .out16(demultiplexer_2_out16), .out17(demultiplexer_2_out17),
    .out18(demultiplexer_2_out18), .out19(demultiplexer_2_out19), .out20(demultiplexer_2_out20),
    .out21(demultiplexer_2_out21), .out22(demultiplexer_2_out22), .out23(demultiplexer_2_out23),
    .out24(demultiplexer_2_out24), .out25(demultiplexer_2_out25), .out26(demultiplexer_2_out26),
    .out27(demultiplexer_2_out27), .out28(demultiplexer_2_out28), .out29(demultiplexer_2_out29),
    .out30(demultiplexer_2_out30), .out31(demultiplexer_2_out31), .in(in_2), .sel(Add_C), .en(Enable_C));
endmodule

module RegisterFile (
  input  [1:0] C_Select,
  input  Clear,
  output [31:0] Display_A,
  output [31:0] Display_B,
  output [31:0] Just_Display
);

  wire Clock_out, cu_1_c_enable, cu_1_immediate_enable, cu_1_load, cu_1_store;
  wire [1:0] cu_1_add_sub_mov;
  wire [4:0] Instruction_Register_q10, Instruction_Register_q15, Instruction_Register_q20, multiplexer_3_out;
  wire [5:0] Instruction_Register_q5;
  wire [10:0] Instruction_Register_q31;
  wire [23:0] bit_extender_1_out;
  wire [31:0] iag_1_pc, memory_1_output_data, multiplexer_1_out, multiplexer_2_out, RA_q31, RB_q31, RM_q31,
       rom_1_data, RY_q31, RZ_q31;

  Clock Clock (.out(Clock_out));
  Shift_Register #(.length(32)) RA (
    .shift(1'b0), .clk(Clock_out), .load(1'b1), .clr(Clear), .d0(Display_A[31]), .q0(RA_q31[31]),
    .d1(Display_A[30]), .q1(RA_q31[30]), .d2(Display_A[29]), .q2(RA_q31[29]), .d3(Display_A[28]),
    .q3(RA_q31[28]), .d4(Display_A[27]), .q4(RA_q31[27]), .d5(Display_A[26]), .q5(RA_q31[26]),
    .d6(Display_A[25]), .q6(RA_q31[25]), .d7(Display_A[24]), .q7(RA_q31[24]), .d8(Display_A[23]),
    .q8(RA_q31[23]), .d9(Display_A[22]), .q9(RA_q31[22]), .d10(Display_A[21]), .q10(RA_q31[21]),
    .d11(Display_A[20]), .q11(RA_q31[20]), .d12(Display_A[19]), .q12(RA_q31[19]), .d13(Display_A[18]),
    .q13(RA_q31[18]), .d14(Display_A[17]), .q14(RA_q31[17]), .d15(Display_A[16]), .q15(RA_q31[16]),
    .d16(Display_A[15]), .q16(RA_q31[15]), .d17(Display_A[14]), .q17(RA_q31[14]), .d18(Display_A[13]),
    .q18(RA_q31[13]), .d19(Display_A[12]), .q19(RA_q31[12]), .d20(Display_A[11]), .q20(RA_q31[11]),
    .d21(Display_A[10]), .q21(RA_q31[10]), .d22(Display_A[9]), .q22(RA_q31[9]), .d23(Display_A[8]),
    .q23(RA_q31[8]), .d24(Display_A[7]), .q24(RA_q31[7]), .d25(Display_A[6]), .q25(RA_q31[6]),
    .d26(Display_A[5]), .q26(RA_q31[5]), .d27(Display_A[4]), .q27(RA_q31[4]), .d28(Display_A[3]),
    .q28(RA_q31[3]), .d29(Display_A[2]), .q29(RA_q31[2]), .d30(Display_A[1]), .q30(RA_q31[1]),
    .d31(Display_A[0]), .q31(RA_q31[0]));  // open: in, out
  Shift_Register #(.length(32)) RZ (
    .shift(1'b0), .clk(Clock_out), .load(1'b1), .clr(Clear), .d0(Just_Display[31]), .q0(RZ_q31[31]),
    .d1(Just_Display[30]), .q1(RZ_q31[30]), .d2(Just_Display[29]), .q2(RZ_q31[29]), .d3(Just_Display[28]),
    .q3(RZ_q31[28]), .d4(Just_Display[27]), .q4(RZ_q31[27]), .d5(Just_Display[26]), .q5(RZ_q31[26]),
    .d6(Just_Display[25]), .q6(RZ_q31[25]), .d7(Just_Display[24]), .q7(RZ_q31[24]), .d8(Just_Display[23]),
    .q8(RZ_q31[23]), .d9(Just_Display[22]), .q9(RZ_q31[22]), .d10(Just_Display[21]), .q10(RZ_q31[21]),
    .d11(Just_Display[20]), .q11(RZ_q31[20]), .d12(Just_Display[19]), .q12(RZ_q31[19]),
    .d13(Just_Display[18]), .q13(RZ_q31[18]), .d14(Just_Display[17]), .q14(RZ_q31[17]),
    .d15(Just_Display[16]), .q15(RZ_q31[16]), .d16(Just_Display[15]), .q16(RZ_q31[15]),
    .d17(Just_Display[14]), .q17(RZ_q31[14]), .d18(Just_Display[13]), .q18(RZ_q31[13]),
    .d19(Just_Display[12]), .q19(RZ_q31[12]), .d20(Just_Display[11]), .q20(RZ_q31[11]),
    .d21(Just_Display[10]), .q21(RZ_q31[10]), .d22(Just_Display[9]), .q22(RZ_q31[9]), .d23(Just_Display[8]),
    .q23(RZ_q31[8]), .d24(Just_Display[7]), .q24(RZ_q31[7]), .d25(Just_Display[6]), .q25(RZ_q31[6]),
    .d26(Just_Display[5]), .q26(RZ_q31[5]), .d27(Just_Display[4]), .q27(RZ_q31[4]), .d28(Just_Display[3]),
    .q28(RZ_q31[3]), .d29(Just_Display[2]), .q29(RZ_q31[2]), .d30(Just_Display[1]), .q30(RZ_q31[1]),
    .d31(Just_Display[0]), .q31(RZ_q31[0]));  // open: in, out
  main main_1 (
    .Clock(Clock_out), .Enable_Add_C(cu_1_c_enable), .in_2(RY_q31), .Enable_C(cu_1_c_enable),
    .Add_C(multiplexer_3_out), .A_value(Display_A), .Add_A(Instruction_Register_q10), .B_value(Display_B),
    .Add_B(Instruction_Register_q15));
  Shift_Register #(.length(32)) RY (
    .shift(1'b0), .clk(Clock_out), .load(1'b1), .clr(Clear), .d0(multiplexer_1_out[31]), .q0(RY_q31[31]),
    .d1(multiplexer_1_out[30]), .q1(RY_q31[30]), .d2(multiplexer_1_out[29]), .q2(RY_q31[29]),
    .d3(multiplexer_1_out[28]), .q3(RY_q31[28]), .d4(multiplexer_1_out[27]), .q4(RY_q31[27]),
    .d5(multiplexer_1_out[26]), .q5(RY_q31[26]), .d6(multiplexer_1_out[25]), .q6(RY_q31[25]),
    .d7(multiplexer_1_out[24]), .q7(RY_q31[24]), .d8(multiplexer_1_out[23]), .q8(RY_q31[23]),
    .d9(multiplexer_1_out[22]), .q9(RY_q31[22]), .d10(multiplexer_1_out[21]), .q10(RY_q31[21]),
    .d11(multiplexer_1_out[20]), .q11(RY_q31[20]), .d12(multiplexer_1_out[19]), .q12(RY_q31[19]),
    .d13(multiplexer_1_out[18]), .q13(RY_q31[18]), .d14(multiplexer_1_out[17]), .q14(RY_q31[17]),
    .d15(multiplexer_1_out[16]), .q15(RY_q31[16]), .d16(multiplexer_1_out[15]), .q16(RY_q31[15]),
    .d17(multiplexer_1_out[14]), .q17(RY_q31[14]), .d18(multiplexer_1_out[13]), .q18(RY_q31[13]),
    .d19(multiplexer_1_out[12]), .q19(RY_q31[12]), .d20(multiplexer_1_out[11]), .q20(RY_q31[11]),
    .d21(multiplexer_1_out[10]), .q21(RY_q31[10]), .d22(multiplexer_1_out[9]), .q22(RY_q31[9]),
    .d23(multiplexer_1_out[8]), .q23(RY_q31[8]), .d24(multiplexer_1_out[7]), .q24(RY_q31[7]),
    .d25(multiplexer_1_out[6]), .q25(RY_q31[6]), .d26(multiplexer_1_out[5]), .q26(RY_q31[5]),
    .d27(multiplexer_1_out[4]), .q27(RY_q31[4]), .d28(multiplexer_1_out[3]), .q28(RY_q31[3]),
    .d29(multiplexer_1_out[2]), .q29(RY_q31[2]), .d30(multiplexer_1_out[1]), .q30(RY_q31[1]),
    .d31(multiplexer_1_out[0]), .q31(RY_q31[0]));  // open: in, out
  Multiplexer #(.width(32), .enable("false")) multiplexer_1 (
    .in0(RZ_q31), .in1(memory_1_output_data), .out(multiplexer_1_out), .sel(cu_1_load));
  Shift_Register #(.length(32)) RB (
    .shift(1'b0), .clk(Clock_out), .load(1'b1), .clr(Clear), .d0(Display_B[31]), .q0(RB_q31[31]),
    .d1(Display_B[30]), .q1(RB_q31[30]), .d2(Display_B[29]), .q2(RB_q31[29]), .d3(Display_B[28]),
    .q3(RB_q31[28]), .d4(Display_B[27]), .q4(RB_q31[27]), .d5(Display_B[26]), .q5(RB_q31[26]),
    .d6(Display_B[25]), .q6(RB_q31[25]), .d7(Display_B[24]), .q7(RB_q31[24]), .d8(Display_B[23]),
    .q8(RB_q31[23]), .d9(Display_B[22]), .q9(RB_q31[22]), .d10(Display_B[21]), .q10(RB_q31[21]),
    .d11(Display_B[20]), .q11(RB_q31[20]), .d12(Display_B[19]), .q12(RB_q31[19]), .d13(Display_B[18]),
    .q13(RB_q31[18]), .d14(Display_B[17]), .q14(RB_q31[17]), .d15(Display_B[16]), .q15(RB_q31[16]),
    .d16(Display_B[15]), .q16(RB_q31[15]), .d17(Display_B[14]), .q17(RB_q31[14]), .d18(Display_B[13]),
    .q18(RB_q31[13]), .d19(Display_B[12]), .q19(RB_q31[12]), .d20(Display_B[11]), .q20(RB_q31[11]),
    .d21(Display_B[10]), .q21(RB_q31[10]), .d22(Display_B[9]), .q22(RB_q31[9]), .d23(Display_B[8]),
    .q23(RB_q31[8]), .d24(Display_B[7]), .q24(RB_q31[7]), .d25(Display_B[6]), .q25(RB_q31[6]),
    .d26(Display_B[5]), .q26(RB_q31[5]), .d27(Display_B[4]), .q27(RB_q31[4]), .d28(Display_B[3]),
    .q28(RB_q31[3]), .d29(Display_B[2]), .q29(RB_q31[2]), .d30(Display_B[1]), .q30(RB_q31[1]),
    .d31(Display_B[0]), .q31(RB_q31[0]));  // open: in, out
  ALU alu_1 (
    .RA(RA_q31), .RB(multiplexer_2_out), .in_4(cu_1_immediate_enable), .ADD_SUB_MOV(cu_1_add_sub_mov),
    .out_5(Just_Display));
  Shift_Register #(.length(32)) RM (
    .shift(1'b0), .clk(Clock_out), .load(1'b1), .clr(Clear), .d0(RB_q31[31]), .q0(RM_q31[31]),
    .d1(RB_q31[30]), .q1(RM_q31[30]), .d2(RB_q31[29]), .q2(RM_q31[29]), .d3(RB_q31[28]), .q3(RM_q31[28]),
    .d4(RB_q31[27]), .q4(RM_q31[27]), .d5(RB_q31[26]), .q5(RM_q31[26]), .d6(RB_q31[25]), .q6(RM_q31[25]),
    .d7(RB_q31[24]), .q7(RM_q31[24]), .d8(RB_q31[23]), .q8(RM_q31[23]), .d9(RB_q31[22]), .q9(RM_q31[22]),
    .d10(RB_q31[21]), .q10(RM_q31[21]), .d11(RB_q31[20]), .q11(RM_q31[20]), .d12(RB_q31[19]),
    .q12(RM_q31[19]), .d13(RB_q31[18]), .q13(RM_q31[18]), .d14(RB_q31[17]), .q14(RM_q31[17]),
    .d15(RB_q31[16]), .q15(RM_q31[16]), .d16(RB_q31[15]), .q16(RM_q31[15]), .d17(RB_q31[14]),
    .q17(RM_q31[14]), .d18(RB_q31[13]), .q18(RM_q31[13]), .d19(RB_q31[12]), .q19(RM_q31[12]),
    .d20(RB_q31[11]), .q20(RM_q31[11]), .d21(RB_q31[10]), .q21(RM_q31[10]), .d22(RB_q31[9]), .q22(RM_q31[9]),
    .d23(RB_q31[8]), .q23(RM_q31[8]), .d24(RB_q31[7]), .q24(RM_q31[7]), .d25(RB_q31[6]), .q25(RM_q31[6]),
    .d26(RB_q31[5]), .q26(RM_q31[5]), .d27(RB_q31[4]), .q27(RM_q31[4]), .d28(RB_q31[3]), .q28(RM_q31[3]),
    .d29(RB_q31[2]), .q29(RM_q31[2]), .d30(RB_q31[1]), .q30(RM_q31[1]), .d31(RB_q31[0]), .q31(RM_q31[0]));  // open: in, out
  Multiplexer #(.width(32), .enable("false")) multiplexer_2 (
    .in0(RB_q31), .in1({{16{1'b0}}, Instruction_Register_q20, Instruction_Register_q31}),
    .out(multiplexer_2_out), .sel(cu_1_immediate_enable));
  MEMORY memory_1 (
    .Address(RZ_q31), .W_data(RM_q31), .Output_data(memory_1_output_data), .store(cu_1_store),
    .clock(Clock_out), .load(cu_1_load), .clear(Clear));
  Multiplexer #(.select(2), .width(5), .enable("false")) multiplexer_3 (
    .in0(Instruction_Register_q10), .in1(Instruction_Register_q15), .in2(Instruction_Register_q20),
    .out(multiplexer_3_out), .sel(C_Select));  // open: in3
  CU cu_1 (
    .Immediate_Enable(cu_1_immediate_enable), .C_Enable(cu_1_c_enable), .ADD_SUB_MOV(cu_1_add_sub_mov),
    .store(cu_1_store), .load(cu_1_load), .in_1(Instruction_Register_q5));
  Shift_Register #(.length(32)) Instruction_Register (
    .shift(1'b0), .clk(Clock_out), .clr(Clear), .d0(rom_1_data[31]), .q0(Instruction_Register_q5[5]),
    .d1(rom_1_data[30]), .q1(Instruction_Register_q5[4]), .d2(rom_1_data[29]),
    .q2(Instruction_Register_q5[3]), .d3(rom_1_data[28]), .q3(Instruction_Register_q5[2]),
    .d4(rom_1_data[27]), .q4(Instruction_Register_q5[1]), .d5(rom_1_data[26]),
    .q5(Instruction_Register_q5[0]), .d6(rom_1_data[25]), .q6(Instruction_Register_q10[4]),
    .d7(rom_1_data[24]), .q7(Instruction_Register_q10[3]), .d8(rom_1_data[23]),
    .q8(Instruction_Register_q10[2]), .d9(rom_1_data[22]), .q9(Instruction_Register_q10[1]),
    .d10(rom_1_data[21]), .q10(Instruction_Register_q10[0]), .d11(rom_1_data[20]),
    .q11(Instruction_Register_q15[4]), .d12(rom_1_data[19]), .q12(Instruction_Register_q15[3]),
    .d13(rom_1_data[18]), .q13(Instruction_Register_q15[2]), .d14(rom_1_data[17]),
    .q14(Instruction_Register_q15[1]), .d15(rom_1_data[16]), .q15(Instruction_Register_q15[0]),
    .d16(rom_1_data[15]), .q16(Instruction_Register_q20[4]), .d17(rom_1_data[14]),
    .q17(Instruction_Register_q20[3]), .d18(rom_1_data[13]), .q18(Instruction_Register_q20[2]),
    .d19(rom_1_data[12]), .q19(Instruction_Register_q20[1]), .d20(rom_1_data[11]),
    .q20(Instruction_Register_q20[0]), .d21(rom_1_data[10]), .q21(Instruction_Register_q31[10]),
    .d22(rom_1_data[9]), .q22(Instruction_Register_q31[9]), .d23(rom_1_data[8]),
    .q23(Instruction_Register_q31[8]), .d24(rom_1_data[7]), .q24(Instruction_Register_q31[7]),
    .d25(rom_1_data[6]), .q25(Instruction_Register_q31[6]), .d26(rom_1_data[5]),
    .q26(Instruction_Register_q31[5]), .d27(rom_1_data[4]), .q27(Instruction_Register_q31[4]),
    .d28(rom_1_data[3]), .q28(Instruction_Register_q31[3]), .d29(rom_1_data[2]),
    .q29(Instruction_Register_q31[2]), .d30(rom_1_data[1]), .q30(Instruction_Register_q31[1]),
    .d31(rom_1_data[0]), .q31(Instruction_Register_q31[0]));  // open: in, out, load
  IAG iag_1 (
    .Clock(Clock_out), .Clear(Clear), .PC_Src(cu_1_immediate_enable), .PC(iag_1_pc),
    .Immediate({{16{1'b0}}, Instruction_Register_q20, Instruction_Register_q31}));
  Bit_Extender #(.in_width(32), .out_width(24)) bit_extender_1 (.in(iag_1_pc), .out(bit_extender_1_out));
  ROM #(.addrWidth(24), .dataWidth(32)) rom_1 (.addr(bit_extender_1_out), .data(rom_1_data), .sel(1'b1));

  // Notes on the sheet:
  //   Register File
  //   MUXY
  //   ALU
  //   MUXB
  //   RAM
  //   MUXC
  //   00 ADD 01 SUB 10 MOV
  //   Control Unit
  //   Instruction Address Generator
  //   ROM
endmodule

module ALU (
  input  [31:0] RA,
  input  [31:0] RB,
  input  [1:0] ADD_SUB_MOV,
  input  in_4,
  output [31:0] out_5
);

  wire [31:0] adder_1_out, multiplexer_1_out, subtractor_1_out;

  Adder #(.width(32)) adder_1 (.a(RA), .b(RB), .out(adder_1_out), .cin(1'b0));  // open: cout
  Subtractor #(.width(32)) subtractor_1 (.a(RA), .b(RB), .out(subtractor_1_out), .bin(1'b0));  // open: bout
  Multiplexer #(.width(32), .enable("false")) multiplexer_1 (.in0(RA), .in1(RB), .out(multiplexer_1_out), .sel(in_4));
  Multiplexer #(.select(2), .width(32), .enable("false")) multiplexer_2 (
    .in0(adder_1_out), .in1(subtractor_1_out), .in2(multiplexer_1_out), .in3(multiplexer_1_out), .out(out_5),
    .sel(ADD_SUB_MOV));
endmodule

module IAG (
  input  Clock,
  input  Clear,
  input  [31:0] Immediate,
  input  PC_Src,
  output [31:0] PC
);

  wire [31:0] adder_1_out, multiplexer_1_out;

  Shift_Register #(.length(32)) u_PC (
    .shift(1'b0), .clk(Clock), .load(1'b1), .clr(Clear), .d0(multiplexer_1_out[31]), .q0(PC[31]),
    .d1(multiplexer_1_out[30]), .q1(PC[30]), .d2(multiplexer_1_out[29]), .q2(PC[29]),
    .d3(multiplexer_1_out[28]), .q3(PC[28]), .d4(multiplexer_1_out[27]), .q4(PC[27]),
    .d5(multiplexer_1_out[26]), .q5(PC[26]), .d6(multiplexer_1_out[25]), .q6(PC[25]),
    .d7(multiplexer_1_out[24]), .q7(PC[24]), .d8(multiplexer_1_out[23]), .q8(PC[23]),
    .d9(multiplexer_1_out[22]), .q9(PC[22]), .d10(multiplexer_1_out[21]), .q10(PC[21]),
    .d11(multiplexer_1_out[20]), .q11(PC[20]), .d12(multiplexer_1_out[19]), .q12(PC[19]),
    .d13(multiplexer_1_out[18]), .q13(PC[18]), .d14(multiplexer_1_out[17]), .q14(PC[17]),
    .d15(multiplexer_1_out[16]), .q15(PC[16]), .d16(multiplexer_1_out[15]), .q16(PC[15]),
    .d17(multiplexer_1_out[14]), .q17(PC[14]), .d18(multiplexer_1_out[13]), .q18(PC[13]),
    .d19(multiplexer_1_out[12]), .q19(PC[12]), .d20(multiplexer_1_out[11]), .q20(PC[11]),
    .d21(multiplexer_1_out[10]), .q21(PC[10]), .d22(multiplexer_1_out[9]), .q22(PC[9]),
    .d23(multiplexer_1_out[8]), .q23(PC[8]), .d24(multiplexer_1_out[7]), .q24(PC[7]),
    .d25(multiplexer_1_out[6]), .q25(PC[6]), .d26(multiplexer_1_out[5]), .q26(PC[5]),
    .d27(multiplexer_1_out[4]), .q27(PC[4]), .d28(multiplexer_1_out[3]), .q28(PC[3]),
    .d29(multiplexer_1_out[2]), .q29(PC[2]), .d30(multiplexer_1_out[1]), .q30(PC[1]),
    .d31(multiplexer_1_out[0]), .q31(PC[0]));  // open: in, out
  Adder #(.width(32)) adder_1 (.a(PC), .b(32'h1), .out(adder_1_out));  // open: cin, cout
  Multiplexer #(.width(32), .enable("false")) multiplexer_1 (
    .in0(adder_1_out), .in1(Immediate), .out(multiplexer_1_out), .sel(PC_Src));
endmodule

module CU (
  input  [5:0] in_1,
  output Immediate_Enable,
  output C_Enable,
  output [1:0] ADD_SUB_MOV,
  output store,
  output load
);

  wire and_1_out, and_2_out, not_2_out;

  and and_1 (and_1_out, in_1[2], in_1[1]);
  and and_2 (and_2_out, in_1[0], in_1[1], in_1[2]);
  and and_3 (store, and_1_out, in_1[0]);
  not not_1 (C_Enable, and_2_out);
  Multiplexer #(.select(2), .width(2), .enable("false")) multiplexer_1 (
    .in0(2'b10), .in1(2'b00), .in2(2'b01), .in3(2'b10), .out(ADD_SUB_MOV), .sel(in_1[2:1]));
  not not_2 (not_2_out, in_1[0]);
  and and_4 (load, and_1_out, not_2_out);

  assign Immediate_Enable = in_1[5];

  // Notes on the sheet:
  //   LSB
  //   MSB
endmodule

module MEMORY (
  input  [31:0] Address,
  input  [31:0] W_data,
  input  store,
  input  clock,
  input  load,
  input  clear,
  output [31:0] Output_data
);

  wire [23:0] bit_extender_1_out;

  Bit_Extender #(.in_width(32), .out_width(24)) bit_extender_1 (.in(Address), .out(bit_extender_1_out));
  RAM #(.addrWidth(24), .dataWidth(32), .bus("separate")) ram_1 (
    .addr(bit_extender_1_out), .din(W_data), .data(Output_data), .str(store), .sel(1'b1), .clk(clock),
    .ld(load), .clr(clear));
endmodule
